// Logisim project 01_MIPS_Processor_PreJump.circ as structural Verilog: 18 circuits, main circuit main
module main (
  input  Reset
);

  wire and_1_out, clock_1_out, controlpathregister2_1_branche, controlpathregister2_1_regdste,
       controlpathregister2_1_regwritee, controlpathregister3_1_branchm, controlpathregister3_1_regwritem,
       controlpathregister4_1_regwritew, controlunit_1_branch, controlunit_1_regdst, controlunit_1_regwrite,
       datapathregister3_1_zerom, nand_1_out;
  wire [1:0] controlpathregister2_1_alusrce, controlpathregister2_1_memtorege,
       controlpathregister3_1_memtoregm, controlpathregister4_1_memtoregw, controlunit_1_alusrc,
       controlunit_1_memtoreg;
  wire [3:0] controlpathregister2_1_alucontrole, controlpathregister2_1_memope,
       controlpathregister3_1_memopm, controlunit_1_alucontrol, controlunit_1_memop;
  wire [4:0] datapathregister2_1_r_rd_e, datapathregister2_1_r_rt_e, datapathregister3_1_writeregm,
       datapathregister4_1_writeregw, multiplexer_4_out;
  wire [31:0] adder_1_out, adder_2_out, alu_1_q, bit_extender_1_out, datapathregister1_1_instrd,
       datapathregister1_1_pcplus4d, datapathregister2_1_pcplus4e, datapathregister2_1_regdata1e,
       datapathregister2_1_regdata2e, datapathregister2_1_signimme, datapathregister3_1_aluoutm,
       datapathregister3_1_pcbranchm, datapathregister3_1_upperimmm, datapathregister3_1_writedatam,
       datapathregister4_1_aluoutw, datapathregister4_1_readdataw, datapathregister4_1_upperimmw,
       mainmemory_1_dataout, multiplexer_1_out, multiplexer_2_out, multiplexer_3_out, multiplexer_5_out,
       multiplexer_6_out, pc_q, registerfile_1_registerdata1, registerfile_1_registerdata2, S1_Fetch_q,
       S2_Decode_q, S3_Execute_q, S4_Memory_q, shifter_1_out, shifter_2_out, textsection_1_instruction,
       undriven;

  Clock clock_1 (.out(clock_1_out));
  Multiplexer #(.width(32)) multiplexer_1 (
    .in0(adder_1_out), .in1(datapathregister3_1_pcbranchm), .out(multiplexer_1_out), .sel(and_1_out));
  Multiplexer #(.width(32)) multiplexer_2 (
    .in0(multiplexer_1_out), .in1(32'h400000), .out(multiplexer_2_out), .sel(Reset));
  Register #(.width(32)) pc (.D(multiplexer_2_out), .clk(clock_1_out), .Q(pc_q));  // open: en, clr
  Adder #(.width(32)) adder_1 (.a(pc_q), .b(32'h4), .out(adder_1_out));  // open: cin, cout
  TextSection textsection_1 (.Address(pc_q), .Instruction(textsection_1_instruction));  // open: InvalidAddressFlag
  Register #(.trigger("low"), .width(32)) S1_Fetch (
    .D(textsection_1_instruction), .clk(clock_1_out), .Q(S1_Fetch_q), .clr(Reset));  // open: en
  Register #(.width(32)) S2_Decode (.D(S1_Fetch_q), .clk(clock_1_out), .Q(S2_Decode_q), .clr(Reset));  // open: en
  DataPathRegister1 datapathregister1_1 (
    .InstrF(textsection_1_instruction), .PCPlus4F(adder_1_out), .CLK(clock_1_out), .Reset(Reset),
    .InstrD(datapathregister1_1_instrd), .PCPlus4D(datapathregister1_1_pcplus4d));
  // Probe on datapathregister1_1_instrd[31:26]
  // Probe on datapathregister1_1_instrd[5:0]
  // Probe on datapathregister1_1_instrd[25:21]
  // Probe on datapathregister1_1_instrd[20:16]
  // Probe on datapathregister1_1_instrd[15:11]
  // Probe on datapathregister1_1_instrd[15:0]
  Register #(.width(32)) S3_Execute (.D(S2_Decode_q), .clk(clock_1_out), .Q(S3_Execute_q), .clr(Reset));  // open: en
  Register #(.width(32)) S4_Memory (.D(S3_Execute_q), .clk(clock_1_out), .Q(S4_Memory_q), .clr(Reset));  // open: en
  ControlUnit controlunit_1 (
    .Op(datapathregister1_1_instrd[31:26]), .Func(datapathregister1_1_instrd[5:0]),
    .RegWrite(controlunit_1_regwrite), .MemToReg(controlunit_1_memtoreg), .MemOp(controlunit_1_memop),
    .Branch(controlunit_1_branch), .ALUControl(controlunit_1_alucontrol), .ALUSrc(controlunit_1_alusrc),
    .RegDst(controlunit_1_regdst));
  RegisterFile registerfile_1 (
    .Address1(datapathregister1_1_instrd[25:21]), .Address2(datapathregister1_1_instrd[20:16]),
    .WriteEnable3(controlpathregister4_1_regwritew), .Address3(datapathregister4_1_writeregw),
    .WriteData3(multiplexer_6_out), .CLK(clock_1_out), .Reset(Reset),
    .RegisterData1(registerfile_1_registerdata1), .RegisterData2(registerfile_1_registerdata2));
  assign bit_extender_1_out = {{16{datapathregister1_1_instrd[15]}}, datapathregister1_1_instrd[15:0]};  // Bit_Extender bit_extender_1
  Register #(.width(32)) S5_Writeback (.D(S4_Memory_q), .clk(clock_1_out), .clr(Reset));  // open: en, Q
  ControlPathRegister2 controlpathregister2_1 (
    .RegWriteD(controlunit_1_regwrite), .MemToRegD(controlunit_1_memtoreg), .MemOpD(controlunit_1_memop),
    .BranchD(controlunit_1_branch), .ALUControlD(controlunit_1_alucontrol), .ALUSrcD(controlunit_1_alusrc),
    .RegDstD(controlunit_1_regdst), .CLK(clock_1_out), .Reset(Reset),
    .RegWriteE(controlpathregister2_1_regwritee), .MemToRegE(controlpathregister2_1_memtorege),
    .MemOpE(controlpathregister2_1_memope), .BranchE(controlpathregister2_1_branche),
    .ALUControlE(controlpathregister2_1_alucontrole), .ALUSrcE(controlpathregister2_1_alusrce),
    .RegDstE(controlpathregister2_1_regdste));
  DataPathRegister2 datapathregister2_1 (
    .RegData1D(registerfile_1_registerdata1), .RegData2D(registerfile_1_registerdata2),
    .r_rt_D(datapathregister1_1_instrd[20:16]), .r_rd_D(datapathregister1_1_instrd[15:11]),
    .SignImmD(bit_extender_1_out), .PCPlus4D(datapathregister1_1_pcplus4d), .CLK(clock_1_out), .Reset(Reset),
    .RegData1E(datapathregister2_1_regdata1e), .RegData2E(datapathregister2_1_regdata2e),
    .r_rt_E(datapathregister2_1_r_rt_e), .r_rd_E(datapathregister2_1_r_rd_e),
    .SignImmE(datapathregister2_1_signimme), .PCPlus4E(datapathregister2_1_pcplus4e));
  nand nand_1 (nand_1_out, controlpathregister2_1_alusrce[1], ~controlpathregister2_1_alusrce[0]);  // NAND_Gate
  Multiplexer #(.width(32)) multiplexer_3 (
    .in0(datapathregister3_1_upperimmm), .in1(datapathregister2_1_regdata1e), .out(multiplexer_3_out),
    .sel(nand_1_out));
  Shifter #(.width(32)) shifter_1 (.in(datapathregister2_1_signimme), .\dist (5'b10000), .out(shifter_1_out));
  Multiplexer #(.width(5)) multiplexer_4 (
    .in0(datapathregister2_1_r_rt_e), .in1(datapathregister2_1_r_rd_e), .out(multiplexer_4_out),
    .sel(controlpathregister2_1_regdste));
  Shifter #(.width(32)) shifter_2 (.in(datapathregister2_1_signimme), .\dist (5'b00010), .out(shifter_2_out));
  // Probe on controlpathregister2_1_alusrce
  Multiplexer #(.select(2), .width(32)) multiplexer_5 (
    .in0(datapathregister2_1_regdata2e), .in1(datapathregister2_1_signimme),
    .in2(datapathregister2_1_signimme), .in3(undriven), .out(multiplexer_5_out),
    .sel(controlpathregister2_1_alusrce));
  // NoConnect on undriven
  Adder #(.width(32)) adder_2 (
    .a(datapathregister2_1_pcplus4e), .b(shifter_2_out), .out(adder_2_out));  // open: cin, cout
  // Probe on controlpathregister2_1_alucontrole
  ALU alu_1 (
    .ALUControl(controlpathregister2_1_alucontrole), .A(multiplexer_3_out), .B(multiplexer_5_out), .Q(alu_1_q));  // open: NOT_ALUOutput
  // Probe on alu_1_q
  // Probe on shifter_1_out
  // Probe on datapathregister2_1_regdata2e
  // Probe on multiplexer_4_out
  // Probe on adder_2_out
  ControlPathRegister3 controlpathregister3_1 (
    .RegWriteE(controlpathregister2_1_regwritee), .MemToRegE(controlpathregister2_1_memtorege),
    .MemOpE(controlpathregister2_1_memope), .BranchE(controlpathregister2_1_branche), .CLK(clock_1_out),
    .Reset(Reset), .RegWriteM(controlpathregister3_1_regwritem),
    .MemToRegM(controlpathregister3_1_memtoregm), .MemOpM(controlpathregister3_1_memopm),
    .BranchM(controlpathregister3_1_branchm));
  and and_1 (and_1_out, controlpathregister3_1_branchm, datapathregister3_1_zerom);
  DataPathRegister3 datapathregister3_1 (
    .ALUOutE(alu_1_q), .UpperImmE(shifter_1_out), .WriteDataE(datapathregister2_1_regdata2e),
    .WriteRegE(multiplexer_4_out), .PCBranchE(adder_2_out), .CLK(clock_1_out), .Reset(Reset),
    .ZeroM(datapathregister3_1_zerom), .ALUOutM(datapathregister3_1_aluoutm),
    .UpperImmM(datapathregister3_1_upperimmm), .WriteDataM(datapathregister3_1_writedatam),
    .WriteRegM(datapathregister3_1_writeregm), .PCBranchM(datapathregister3_1_pcbranchm));
  MainMemory mainmemory_1 (
    .Address(datapathregister3_1_aluoutm), .DataIn(datapathregister3_1_writedatam),
    .MemOp(controlpathregister3_1_memopm), .CLK(clock_1_out), .DataOut(mainmemory_1_dataout));  // open: AdES_AddressErrorException
  // Probe on mainmemory_1_dataout
  // Probe on datapathregister3_1_upperimmm
  // Probe on datapathregister3_1_aluoutm
  // Probe on datapathregister3_1_writeregm
  ControlPathRegister4 controlpathregister4_1 (
    .RegWriteM(controlpathregister3_1_regwritem), .MemToRegM(controlpathregister3_1_memtoregm),
    .CLK(clock_1_out), .Reset(Reset), .RegWriteW(controlpathregister4_1_regwritew),
    .MemToRegW(controlpathregister4_1_memtoregw));
  DataPathRegister4 datapathregister4_1 (
    .ALUOutM(datapathregister3_1_aluoutm), .UpperImmM(datapathregister3_1_upperimmm),
    .ReadDataM(mainmemory_1_dataout), .WriteRegM(datapathregister3_1_writeregm), .CLK(clock_1_out),
    .Reset(Reset), .ALUOutW(datapathregister4_1_aluoutw), .UpperImmW(datapathregister4_1_upperimmw),
    .ReadDataW(datapathregister4_1_readdataw), .WriteRegW(datapathregister4_1_writeregw));
  Multiplexer #(.select(2), .width(32)) multiplexer_6 (
    .in0(datapathregister4_1_aluoutw), .in1(datapathregister4_1_readdataw),
    .in2(datapathregister4_1_upperimmw), .out(multiplexer_6_out), .sel(controlpathregister4_1_memtoregw));  // open: in3
  // Probe on multiplexer_6_out
  // Probe on datapathregister4_1_writeregw

  // Notes on the sheet:
  //   PC Reset Value
  //   PCSrcM
  //   0 - PC + 4
  //   1 - PCBranch Addr
  //   Reset
  //   0 - No Change
  //   1 - PC Reset Value
  //   op [31:26]
  //   funct [5:0]
  //   RegWriteW ->
  //   rs [25:21]
  //   rt [20:16]
  //   rt [20:16]
  //   rd [15:11]
  //   imm [15:0]
  //   **Note: Registers in the RegisterFile are
  //   written to on FALLING edges of the clock.
  //   Therefore, the instruction in S5 will not have register
  //   writeback shown until the clock returns to LOW.
  //   Data-Forwarding for Addiu -->
  //   (after lui)
  //   Reverse-Direction Control Path
  //   ALUSrcE
  //   ZeroM
  //   PCSrcM
  //   MemToRegW
endmodule

module ControlUnit (
  input  [5:0] Op,
  input  [5:0] Func,
  output RegWrite,
  output [1:0] MemToReg,
  output [3:0] MemOp,
  output Branch,
  output [3:0] ALUControl,
  output [1:0] ALUSrc,
  output RegDst
);

  wire [3:0] maindecoder_1_aluop;

  MainDecoder maindecoder_1 (
    .Op(Op), .RegWrite(RegWrite), .MemToReg(MemToReg), .MemOp(MemOp), .Branch(Branch),
    .ALUOp(maindecoder_1_aluop), .ALUSrc(ALUSrc), .RegDst(RegDst));
  ALUDecoder aludecoder_1 (.ALUOp(maindecoder_1_aluop), .Func(Func), .ALUControl(ALUControl));  // open: NOT_ALUOut

  // Notes on the sheet:
  //   **Note: ALUSrc = 0b10 when lui instruction occurrs,
  //   this makes the A input to ALU be SignImm
endmodule

module MainDecoder (
  input  [5:0] Op,
  output RegWrite,
  output [1:0] MemToReg,
  output [3:0] MemOp,
  output Branch,
  output [3:0] ALUOp,
  output [1:0] ALUSrc,
  output RegDst
);

  wire and_1_out, and_2_out, and_3_out, and_4_out, and_5_out, and_6_out, and_7_out, and_8_out, and_9_out,
       and_10_out, and_11_out, and_12_out, and_13_out, and_14_out, and_15_out, and_16_out, and_17_out,
       and_18_out, and_19_out, and_20_out, and_21_out, and_22_out, and_23_out, and_24_out, and_25_out,
       and_26_out, and_27_out, and_28_out, and_29_out, and_30_out, and_31_out, and_32_out, and_33_out,
       and_34_out, and_35_out, and_36_out, and_37_out, and_38_out, and_39_out, and_40_out, and_41_out,
       and_42_out, and_43_out, and_44_out, and_45_out, and_46_out, and_47_out, and_48_out, and_49_out,
       and_50_out, and_51_out, and_52_out, and_53_out, and_54_out, and_55_out, and_56_out, and_57_out,
       and_58_out, and_59_out, and_60_out, and_61_out, and_62_out, and_63_out, and_64_out;
  wire [14:0] and_65_out, and_66_out, and_67_out, and_68_out, and_69_out, and_70_out, and_71_out, and_72_out,
       and_73_out, and_74_out, and_75_out, and_76_out, and_77_out, and_78_out, and_79_out, and_80_out,
       and_81_out, and_82_out, and_83_out, and_84_out, and_85_out, and_86_out, and_87_out, and_88_out,
       and_89_out, and_90_out, and_91_out, and_92_out, and_93_out, and_94_out, and_95_out, and_96_out,
       and_97_out, and_98_out, and_99_out, and_100_out, and_101_out, and_102_out, and_103_out, and_104_out,
       and_105_out, and_106_out, and_107_out, and_108_out, and_109_out, and_110_out, and_111_out,
       and_112_out, and_113_out, and_114_out, and_115_out, and_116_out, and_117_out, and_118_out,
       and_119_out, and_120_out, and_121_out, and_122_out, and_123_out, and_124_out, and_125_out,
       and_126_out, and_127_out, and_128_out, bit_extender_1_out, bit_extender_2_out, bit_extender_3_out,
       bit_extender_4_out, bit_extender_5_out, bit_extender_6_out, bit_extender_7_out, bit_extender_8_out,
       bit_extender_9_out, bit_extender_10_out, bit_extender_11_out, bit_extender_12_out,
       bit_extender_13_out, bit_extender_14_out, bit_extender_15_out, bit_extender_16_out,
       bit_extender_17_out, bit_extender_18_out, bit_extender_19_out, bit_extender_20_out,
       bit_extender_21_out, bit_extender_22_out, bit_extender_23_out, bit_extender_24_out,
       bit_extender_25_out, bit_extender_26_out, bit_extender_27_out, bit_extender_28_out,
       bit_extender_29_out, bit_extender_30_out, bit_extender_31_out, bit_extender_32_out,
       bit_extender_33_out, bit_extender_34_out, bit_extender_35_out, bit_extender_36_out,
       bit_extender_37_out, bit_extender_38_out, bit_extender_39_out, bit_extender_40_out,
       bit_extender_41_out, bit_extender_42_out, bit_extender_43_out, bit_extender_44_out,
       bit_extender_45_out, bit_extender_46_out, bit_extender_47_out, bit_extender_48_out,
       bit_extender_49_out, bit_extender_50_out, bit_extender_51_out, bit_extender_52_out,
       bit_extender_53_out, bit_extender_54_out, bit_extender_55_out, bit_extender_56_out,
       bit_extender_57_out, bit_extender_58_out, bit_extender_59_out, bit_extender_60_out,
       bit_extender_61_out, bit_extender_62_out, bit_extender_63_out, bit_extender_64_out, or_2_out,
       or_3_out, or_4_out, or_5_out, or_6_out, or_7_out, or_8_out, or_9_out, or_10_out, or_11_out, or_12_out,
       or_13_out, or_14_out, or_15_out, or_16_out, or_17_out, or_18_out, or_19_out, or_20_out, or_21_out,
       or_22_out, or_23_out, or_24_out, or_25_out, or_26_out, or_27_out, or_28_out, or_29_out, or_30_out,
       or_31_out, or_32_out, or_33_out, or_34_out, or_35_out, or_36_out, or_37_out, or_38_out, or_39_out,
       or_40_out, or_41_out, or_42_out, or_43_out, or_44_out, or_45_out, or_46_out, or_47_out, or_48_out,
       or_49_out, or_50_out, or_51_out, or_52_out, or_53_out, or_54_out, or_55_out, or_56_out, or_57_out,
       or_58_out, or_59_out, or_60_out, or_61_out, or_62_out, or_63_out, or_64_out;

  and and_1 (and_1_out, ~Op[5], ~Op[4], ~Op[3], ~Op[2], ~Op[1], ~Op[0]);  // AND_Gate
  and and_2 (and_2_out, ~Op[5], ~Op[4], ~Op[3], ~Op[2], ~Op[1], Op[0]);  // AND_Gate
  and and_3 (and_3_out, ~Op[5], ~Op[4], ~Op[3], ~Op[2], Op[1], ~Op[0]);  // AND_Gate
  and and_4 (and_4_out, ~Op[5], ~Op[4], ~Op[3], ~Op[2], Op[1], Op[0]);  // AND_Gate
  and and_5 (and_5_out, ~Op[5], ~Op[4], ~Op[3], Op[2], ~Op[1], ~Op[0]);  // AND_Gate
  and and_6 (and_6_out, ~Op[5], ~Op[4], ~Op[3], Op[2], ~Op[1], Op[0]);  // AND_Gate
  and and_7 (and_7_out, ~Op[5], ~Op[4], ~Op[3], Op[2], Op[1], ~Op[0]);  // AND_Gate
  and and_8 (and_8_out, ~Op[5], ~Op[4], ~Op[3], Op[2], Op[1], Op[0]);  // AND_Gate
  and and_9 (and_9_out, ~Op[5], ~Op[4], Op[3], ~Op[2], ~Op[1], ~Op[0]);  // AND_Gate
  and and_10 (and_10_out, ~Op[5], ~Op[4], Op[3], ~Op[2], ~Op[1], Op[0]);  // AND_Gate
  and and_11 (and_11_out, ~Op[5], ~Op[4], Op[3], ~Op[2], Op[1], ~Op[0]);  // AND_Gate
  and and_12 (and_12_out, ~Op[5], ~Op[4], Op[3], ~Op[2], Op[1], Op[0]);  // AND_Gate
  and and_13 (and_13_out, ~Op[5], ~Op[4], Op[3], Op[2], ~Op[1], ~Op[0]);  // AND_Gate
  and and_14 (and_14_out, ~Op[5], ~Op[4], Op[3], Op[2], ~Op[1], Op[0]);  // AND_Gate
  and and_15 (and_15_out, ~Op[5], ~Op[4], Op[3], Op[2], Op[1], ~Op[0]);  // AND_Gate
  and and_16 (and_16_out, ~Op[5], ~Op[4], Op[3], Op[2], Op[1], Op[0]);  // AND_Gate
  and and_17 (and_17_out, ~Op[5], Op[4], ~Op[3], ~Op[2], ~Op[1], ~Op[0]);  // AND_Gate
  and and_18 (and_18_out, ~Op[5], Op[4], ~Op[3], ~Op[2], ~Op[1], Op[0]);  // AND_Gate
  and and_19 (and_19_out, ~Op[5], Op[4], ~Op[3], ~Op[2], Op[1], ~Op[0]);  // AND_Gate
  and and_20 (and_20_out, ~Op[5], Op[4], ~Op[3], ~Op[2], Op[1], Op[0]);  // AND_Gate
  and and_21 (and_21_out, ~Op[5], Op[4], ~Op[3], Op[2], ~Op[1], ~Op[0]);  // AND_Gate
  and and_22 (and_22_out, ~Op[5], Op[4], ~Op[3], Op[2], ~Op[1], Op[0]);  // AND_Gate
  and and_23 (and_23_out, ~Op[5], Op[4], ~Op[3], Op[2], Op[1], ~Op[0]);  // AND_Gate
  and and_24 (and_24_out, ~Op[5], Op[4], ~Op[3], Op[2], Op[1], Op[0]);  // AND_Gate
  and and_25 (and_25_out, ~Op[5], Op[4], Op[3], ~Op[2], ~Op[1], ~Op[0]);  // AND_Gate
  and and_26 (and_26_out, ~Op[5], Op[4], Op[3], ~Op[2], ~Op[1], Op[0]);  // AND_Gate
  and and_27 (and_27_out, ~Op[5], Op[4], Op[3], ~Op[2], Op[1], ~Op[0]);  // AND_Gate
  and and_28 (and_28_out, ~Op[5], Op[4], Op[3], ~Op[2], Op[1], Op[0]);  // AND_Gate
  and and_29 (and_29_out, ~Op[5], Op[4], Op[3], Op[2], ~Op[1], ~Op[0]);  // AND_Gate
  and and_30 (and_30_out, ~Op[5], Op[4], Op[3], Op[2], ~Op[1], Op[0]);  // AND_Gate
  and and_31 (and_31_out, ~Op[5], Op[4], Op[3], Op[2], Op[1], ~Op[0]);  // AND_Gate
  and and_32 (and_32_out, ~Op[5], Op[4], Op[3], Op[2], Op[1], Op[0]);  // AND_Gate
  and and_33 (and_33_out, Op[5], ~Op[4], ~Op[3], ~Op[2], ~Op[1], ~Op[0]);  // AND_Gate
  and and_34 (and_34_out, Op[5], ~Op[4], ~Op[3], ~Op[2], ~Op[1], Op[0]);  // AND_Gate
  and and_35 (and_35_out, Op[5], ~Op[4], ~Op[3], ~Op[2], Op[1], ~Op[0]);  // AND_Gate
  and and_36 (and_36_out, Op[5], ~Op[4], ~Op[3], ~Op[2], Op[1], Op[0]);  // AND_Gate
  and and_37 (and_37_out, Op[5], ~Op[4], ~Op[3], Op[2], ~Op[1], ~Op[0]);  // AND_Gate
  and and_38 (and_38_out, Op[5], ~Op[4], ~Op[3], Op[2], ~Op[1], Op[0]);  // AND_Gate
  and and_39 (and_39_out, Op[5], ~Op[4], ~Op[3], Op[2], Op[1], ~Op[0]);  // AND_Gate
  and and_40 (and_40_out, Op[5], ~Op[4], ~Op[3], Op[2], Op[1], Op[0]);  // AND_Gate
  and and_41 (and_41_out, Op[5], ~Op[4], Op[3], ~Op[2], ~Op[1], ~Op[0]);  // AND_Gate
  and and_42 (and_42_out, Op[5], ~Op[4], Op[3], ~Op[2], ~Op[1], Op[0]);  // AND_Gate
  and and_43 (and_43_out, Op[5], ~Op[4], Op[3], ~Op[2], Op[1], ~Op[0]);  // AND_Gate
  and and_44 (and_44_out, Op[5], ~Op[4], Op[3], ~Op[2], Op[1], Op[0]);  // AND_Gate
  and and_45 (and_45_out, Op[5], ~Op[4], Op[3], Op[2], ~Op[1], ~Op[0]);  // AND_Gate
  and and_46 (and_46_out, Op[5], ~Op[4], Op[3], Op[2], ~Op[1], Op[0]);  // AND_Gate
  and and_47 (and_47_out, Op[5], ~Op[4], Op[3], Op[2], Op[1], ~Op[0]);  // AND_Gate
  and and_48 (and_48_out, Op[5], ~Op[4], Op[3], Op[2], Op[1], Op[0]);  // AND_Gate
  and and_49 (and_49_out, Op[5], Op[4], ~Op[3], ~Op[2], ~Op[1], ~Op[0]);  // AND_Gate
  and and_50 (and_50_out, Op[5], Op[4], ~Op[3], ~Op[2], ~Op[1], Op[0]);  // AND_Gate
  and and_51 (and_51_out, Op[5], Op[4], ~Op[3], ~Op[2], Op[1], ~Op[0]);  // AND_Gate
  and and_52 (and_52_out, Op[5], Op[4], ~Op[3], ~Op[2], Op[1], Op[0]);  // AND_Gate
  and and_53 (and_53_out, Op[5], Op[4], ~Op[3], Op[2], ~Op[1], ~Op[0]);  // AND_Gate
  and and_54 (and_54_out, Op[5], Op[4], ~Op[3], Op[2], ~Op[1], Op[0]);  // AND_Gate
  and and_55 (and_55_out, Op[5], Op[4], ~Op[3], Op[2], Op[1], ~Op[0]);  // AND_Gate
  and and_56 (and_56_out, Op[5], Op[4], ~Op[3], Op[2], Op[1], Op[0]);  // AND_Gate
  and and_57 (and_57_out, Op[5], Op[4], Op[3], ~Op[2], ~Op[1], ~Op[0]);  // AND_Gate
  and and_58 (and_58_out, Op[5], Op[4], Op[3], ~Op[2], ~Op[1], Op[0]);  // AND_Gate
  and and_59 (and_59_out, Op[5], Op[4], Op[3], ~Op[2], Op[1], ~Op[0]);  // AND_Gate
  and and_60 (and_60_out, Op[5], Op[4], Op[3], ~Op[2], Op[1], Op[0]);  // AND_Gate
  and and_61 (and_61_out, Op[5], Op[4], Op[3], Op[2], ~Op[1], ~Op[0]);  // AND_Gate
  and and_62 (and_62_out, Op[5], Op[4], Op[3], Op[2], ~Op[1], Op[0]);  // AND_Gate
  and and_63 (and_63_out, Op[5], Op[4], Op[3], Op[2], Op[1], ~Op[0]);  // AND_Gate
  and and_64 (and_64_out, Op[5], Op[4], Op[3], Op[2], Op[1], Op[0]);
  assign bit_extender_1_out = {{14{and_1_out}}, and_1_out};  // Bit_Extender bit_extender_1
  assign bit_extender_2_out = {{14{and_2_out}}, and_2_out};  // Bit_Extender bit_extender_2
  assign bit_extender_3_out = {{14{and_3_out}}, and_3_out};  // Bit_Extender bit_extender_3
  assign bit_extender_4_out = {{14{and_4_out}}, and_4_out};  // Bit_Extender bit_extender_4
  assign bit_extender_5_out = {{14{and_5_out}}, and_5_out};  // Bit_Extender bit_extender_5
  assign bit_extender_6_out = {{14{and_6_out}}, and_6_out};  // Bit_Extender bit_extender_6
  assign bit_extender_7_out = {{14{and_7_out}}, and_7_out};  // Bit_Extender bit_extender_7
  assign bit_extender_8_out = {{14{and_8_out}}, and_8_out};  // Bit_Extender bit_extender_8
  assign bit_extender_9_out = {{14{and_9_out}}, and_9_out};  // Bit_Extender bit_extender_9
  assign bit_extender_10_out = {{14{and_10_out}}, and_10_out};  // Bit_Extender bit_extender_10
  assign bit_extender_11_out = {{14{and_11_out}}, and_11_out};  // Bit_Extender bit_extender_11
  assign bit_extender_12_out = {{14{and_12_out}}, and_12_out};  // Bit_Extender bit_extender_12
  assign bit_extender_13_out = {{14{and_13_out}}, and_13_out};  // Bit_Extender bit_extender_13
  assign bit_extender_14_out = {{14{and_14_out}}, and_14_out};  // Bit_Extender bit_extender_14
  assign bit_extender_15_out = {{14{and_15_out}}, and_15_out};  // Bit_Extender bit_extender_15
  assign bit_extender_16_out = {{14{and_16_out}}, and_16_out};  // Bit_Extender bit_extender_16
  assign bit_extender_17_out = {{14{and_17_out}}, and_17_out};  // Bit_Extender bit_extender_17
  assign bit_extender_18_out = {{14{and_18_out}}, and_18_out};  // Bit_Extender bit_extender_18
  assign bit_extender_19_out = {{14{and_19_out}}, and_19_out};  // Bit_Extender bit_extender_19
  assign bit_extender_20_out = {{14{and_20_out}}, and_20_out};  // Bit_Extender bit_extender_20
  assign bit_extender_21_out = {{14{and_21_out}}, and_21_out};  // Bit_Extender bit_extender_21
  assign bit_extender_22_out = {{14{and_22_out}}, and_22_out};  // Bit_Extender bit_extender_22
  assign bit_extender_23_out = {{14{and_23_out}}, and_23_out};  // Bit_Extender bit_extender_23
  assign bit_extender_24_out = {{14{and_24_out}}, and_24_out};  // Bit_Extender bit_extender_24
  assign bit_extender_25_out = {{14{and_25_out}}, and_25_out};  // Bit_Extender bit_extender_25
  assign bit_extender_26_out = {{14{and_26_out}}, and_26_out};  // Bit_Extender bit_extender_26
  assign bit_extender_27_out = {{14{and_27_out}}, and_27_out};  // Bit_Extender bit_extender_27
  assign bit_extender_28_out = {{14{and_28_out}}, and_28_out};  // Bit_Extender bit_extender_28
  assign bit_extender_29_out = {{14{and_29_out}}, and_29_out};  // Bit_Extender bit_extender_29
  assign bit_extender_30_out = {{14{and_30_out}}, and_30_out};  // Bit_Extender bit_extender_30
  assign bit_extender_31_out = {{14{and_31_out}}, and_31_out};  // Bit_Extender bit_extender_31
  assign bit_extender_32_out = {{14{and_32_out}}, and_32_out};  // Bit_Extender bit_extender_32
  assign bit_extender_33_out = {{14{and_33_out}}, and_33_out};  // Bit_Extender bit_extender_33
  assign bit_extender_34_out = {{14{and_34_out}}, and_34_out};  // Bit_Extender bit_extender_34
  assign bit_extender_35_out = {{14{and_35_out}}, and_35_out};  // Bit_Extender bit_extender_35
  assign bit_extender_36_out = {{14{and_36_out}}, and_36_out};  // Bit_Extender bit_extender_36
  assign bit_extender_37_out = {{14{and_37_out}}, and_37_out};  // Bit_Extender bit_extender_37
  assign bit_extender_38_out = {{14{and_38_out}}, and_38_out};  // Bit_Extender bit_extender_38
  assign bit_extender_39_out = {{14{and_39_out}}, and_39_out};  // Bit_Extender bit_extender_39
  assign bit_extender_40_out = {{14{and_40_out}}, and_40_out};  // Bit_Extender bit_extender_40
  assign bit_extender_41_out = {{14{and_41_out}}, and_41_out};  // Bit_Extender bit_extender_41
  assign bit_extender_42_out = {{14{and_42_out}}, and_42_out};  // Bit_Extender bit_extender_42
  assign bit_extender_43_out = {{14{and_43_out}}, and_43_out};  // Bit_Extender bit_extender_43
  assign bit_extender_44_out = {{14{and_44_out}}, and_44_out};  // Bit_Extender bit_extender_44
  assign bit_extender_45_out = {{14{and_45_out}}, and_45_out};  // Bit_Extender bit_extender_45
  assign bit_extender_46_out = {{14{and_46_out}}, and_46_out};  // Bit_Extender bit_extender_46
  assign bit_extender_47_out = {{14{and_47_out}}, and_47_out};  // Bit_Extender bit_extender_47
  assign bit_extender_48_out = {{14{and_48_out}}, and_48_out};  // Bit_Extender bit_extender_48
  assign bit_extender_49_out = {{14{and_49_out}}, and_49_out};  // Bit_Extender bit_extender_49
  assign bit_extender_50_out = {{14{and_50_out}}, and_50_out};  // Bit_Extender bit_extender_50
  assign bit_extender_51_out = {{14{and_51_out}}, and_51_out};  // Bit_Extender bit_extender_51
  assign bit_extender_52_out = {{14{and_52_out}}, and_52_out};  // Bit_Extender bit_extender_52
  assign bit_extender_53_out = {{14{and_53_out}}, and_53_out};  // Bit_Extender bit_extender_53
  assign bit_extender_54_out = {{14{and_54_out}}, and_54_out};  // Bit_Extender bit_extender_54
  assign bit_extender_55_out = {{14{and_55_out}}, and_55_out};  // Bit_Extender bit_extender_55
  assign bit_extender_56_out = {{14{and_56_out}}, and_56_out};  // Bit_Extender bit_extender_56
  assign bit_extender_57_out = {{14{and_57_out}}, and_57_out};  // Bit_Extender bit_extender_57
  assign bit_extender_58_out = {{14{and_58_out}}, and_58_out};  // Bit_Extender bit_extender_58
  assign bit_extender_59_out = {{14{and_59_out}}, and_59_out};  // Bit_Extender bit_extender_59
  assign bit_extender_60_out = {{14{and_60_out}}, and_60_out};  // Bit_Extender bit_extender_60
  assign bit_extender_61_out = {{14{and_61_out}}, and_61_out};  // Bit_Extender bit_extender_61
  assign bit_extender_62_out = {{14{and_62_out}}, and_62_out};  // Bit_Extender bit_extender_62
  assign bit_extender_63_out = {{14{and_63_out}}, and_63_out};  // Bit_Extender bit_extender_63
  assign bit_extender_64_out = {{14{and_64_out}}, and_64_out};  // Bit_Extender bit_extender_64
  assign and_65_out = 15'h4041 & bit_extender_1_out;  // AND_Gate and_65, 15 bits wide
  assign and_66_out = {15{1'b0}} & bit_extender_2_out;  // AND_Gate and_66, 15 bits wide
  assign and_67_out = {15{1'b0}} & bit_extender_3_out;  // AND_Gate and_67, 15 bits wide
  assign and_68_out = {15{1'b0}} & bit_extender_4_out;  // AND_Gate and_68, 15 bits wide
  assign and_69_out = 15'h90 & bit_extender_5_out;  // AND_Gate and_69, 15 bits wide
  assign and_70_out = {15{1'b0}} & bit_extender_6_out;  // AND_Gate and_70, 15 bits wide
  assign and_71_out = {15{1'b0}} & bit_extender_7_out;  // AND_Gate and_71, 15 bits wide
  assign and_72_out = {15{1'b0}} & bit_extender_8_out;  // AND_Gate and_72, 15 bits wide
  assign and_73_out = 15'h4002 & bit_extender_9_out;  // AND_Gate and_73, 15 bits wide
  assign and_74_out = 15'h400c & bit_extender_10_out;  // AND_Gate and_74, 15 bits wide
  assign and_75_out = 15'h401a & bit_extender_11_out;  // AND_Gate and_75, 15 bits wide
  assign and_76_out = 15'h4022 & bit_extender_12_out;  // AND_Gate and_76, 15 bits wide
  assign and_77_out = 15'h402a & bit_extender_13_out;  // AND_Gate and_77, 15 bits wide
  assign and_78_out = 15'h4032 & bit_extender_14_out;  // AND_Gate and_78, 15 bits wide
  assign and_79_out = 15'h403a & bit_extender_15_out;  // AND_Gate and_79, 15 bits wide
  assign and_80_out = 15'h6000 & bit_extender_16_out;  // AND_Gate and_80, 15 bits wide
  assign and_81_out = {15{1'b0}} & bit_extender_17_out;  // AND_Gate and_81, 15 bits wide
  assign and_82_out = {15{1'b0}} & bit_extender_18_out;  // AND_Gate and_82, 15 bits wide
  assign and_83_out = {15{1'b0}} & bit_extender_19_out;  // AND_Gate and_83, 15 bits wide
  assign and_84_out = {15{1'b0}} & bit_extender_20_out;  // AND_Gate and_84, 15 bits wide
  assign and_85_out = {15{1'b0}} & bit_extender_21_out;  // AND_Gate and_85, 15 bits wide
  assign and_86_out = {15{1'b0}} & bit_extender_22_out;  // AND_Gate and_86, 15 bits wide
  assign and_87_out = {15{1'b0}} & bit_extender_23_out;  // AND_Gate and_87, 15 bits wide
  assign and_88_out = {15{1'b0}} & bit_extender_24_out;  // AND_Gate and_88, 15 bits wide
  assign and_89_out = {15{1'b0}} & bit_extender_25_out;  // AND_Gate and_89, 15 bits wide
  assign and_90_out = {15{1'b0}} & bit_extender_26_out;  // AND_Gate and_90, 15 bits wide
  assign and_91_out = {15{1'b0}} & bit_extender_27_out;  // AND_Gate and_91, 15 bits wide
  assign and_92_out = {15{1'b0}} & bit_extender_28_out;  // AND_Gate and_92, 15 bits wide
  assign and_93_out = {15{1'b0}} & bit_extender_29_out;  // AND_Gate and_93, 15 bits wide
  assign and_94_out = {15{1'b0}} & bit_extender_30_out;  // AND_Gate and_94, 15 bits wide
  assign and_95_out = {15{1'b0}} & bit_extender_31_out;  // AND_Gate and_95, 15 bits wide
  assign and_96_out = {15{1'b0}} & bit_extender_32_out;  // AND_Gate and_96, 15 bits wide
  assign and_97_out = 15'h5002 & bit_extender_33_out;  // AND_Gate and_97, 15 bits wide
  assign and_98_out = 15'h5102 & bit_extender_34_out;  // AND_Gate and_98, 15 bits wide
  assign and_99_out = 15'h5602 & bit_extender_35_out;  // AND_Gate and_99, 15 bits wide
  assign and_100_out = 15'h5202 & bit_extender_36_out;  // AND_Gate and_100, 15 bits wide
  assign and_101_out = 15'h5402 & bit_extender_37_out;  // AND_Gate and_101, 15 bits wide
  assign and_102_out = 15'h5502 & bit_extender_38_out;  // AND_Gate and_102, 15 bits wide
  assign and_103_out = 15'h5702 & bit_extender_39_out;  // AND_Gate and_103, 15 bits wide
  assign and_104_out = {15{1'b0}} & bit_extender_40_out;  // AND_Gate and_104, 15 bits wide
  assign and_105_out = 15'h802 & bit_extender_41_out;  // AND_Gate and_105, 15 bits wide
  assign and_106_out = 15'h902 & bit_extender_42_out;  // AND_Gate and_106, 15 bits wide
  assign and_107_out = 15'he02 & bit_extender_43_out;  // AND_Gate and_107, 15 bits wide
  assign and_108_out = 15'ha02 & bit_extender_44_out;  // AND_Gate and_108, 15 bits wide
  assign and_109_out = {15{1'b0}} & bit_extender_45_out;  // AND_Gate and_109, 15 bits wide
  assign and_110_out = {15{1'b0}} & bit_extender_46_out;  // AND_Gate and_110, 15 bits wide
  assign and_111_out = 15'hf02 & bit_extender_47_out;  // AND_Gate and_111, 15 bits wide
  assign and_112_out = {15{1'b0}} & bit_extender_48_out;  // AND_Gate and_112, 15 bits wide
  assign and_113_out = {15{1'b0}} & bit_extender_49_out;  // AND_Gate and_113, 15 bits wide
  assign and_114_out = {15{1'b0}} & bit_extender_50_out;  // AND_Gate and_114, 15 bits wide
  assign and_115_out = {15{1'b0}} & bit_extender_51_out;  // AND_Gate and_115, 15 bits wide
  assign and_116_out = {15{1'b0}} & bit_extender_52_out;  // AND_Gate and_116, 15 bits wide
  assign and_117_out = {15{1'b0}} & bit_extender_53_out;  // AND_Gate and_117, 15 bits wide
  assign and_118_out = {15{1'b0}} & bit_extender_54_out;  // AND_Gate and_118, 15 bits wide
  assign and_119_out = {15{1'b0}} & bit_extender_55_out;  // AND_Gate and_119, 15 bits wide
  assign and_120_out = {15{1'b0}} & bit_extender_56_out;  // AND_Gate and_120, 15 bits wide
  assign and_121_out = {15{1'b0}} & bit_extender_57_out;  // AND_Gate and_121, 15 bits wide
  assign and_122_out = {15{1'b0}} & bit_extender_58_out;  // AND_Gate and_122, 15 bits wide
  assign and_123_out = {15{1'b0}} & bit_extender_59_out;  // AND_Gate and_123, 15 bits wide
  assign and_124_out = {15{1'b0}} & bit_extender_60_out;  // AND_Gate and_124, 15 bits wide
  assign and_125_out = {15{1'b0}} & bit_extender_61_out;  // AND_Gate and_125, 15 bits wide
  assign and_126_out = {15{1'b0}} & bit_extender_62_out;  // AND_Gate and_126, 15 bits wide
  assign and_127_out = {15{1'b0}} & bit_extender_63_out;  // AND_Gate and_127, 15 bits wide
  assign and_128_out = {15{1'b0}} & bit_extender_64_out;  // AND_Gate and_128, 15 bits wide
  assign {RegWrite, MemToReg, MemOp, Branch, ALUOp, ALUSrc, RegDst} = and_65_out | or_2_out;  // OR_Gate or_1, 15 bits wide
  assign or_2_out = and_66_out | or_3_out;  // OR_Gate or_2, 15 bits wide
  assign or_3_out = and_67_out | or_4_out;  // OR_Gate or_3, 15 bits wide
  assign or_4_out = and_68_out | or_5_out;  // OR_Gate or_4, 15 bits wide
  assign or_5_out = and_69_out | or_6_out;  // OR_Gate or_5, 15 bits wide
  assign or_6_out = and_70_out | or_7_out;  // OR_Gate or_6, 15 bits wide
  assign or_7_out = and_71_out | or_8_out;  // OR_Gate or_7, 15 bits wide
  assign or_8_out = and_72_out | or_9_out;  // OR_Gate or_8, 15 bits wide
  assign or_9_out = and_73_out | or_10_out;  // OR_Gate or_9, 15 bits wide
  assign or_10_out = and_74_out | or_11_out;  // OR_Gate or_10, 15 bits wide
  assign or_11_out = and_75_out | or_12_out;  // OR_Gate or_11, 15 bits wide
  assign or_12_out = and_76_out | or_13_out;  // OR_Gate or_12, 15 bits wide
  assign or_13_out = and_77_out | or_14_out;  // OR_Gate or_13, 15 bits wide
  assign or_14_out = and_78_out | or_15_out;  // OR_Gate or_14, 15 bits wide
  assign or_15_out = and_79_out | or_16_out;  // OR_Gate or_15, 15 bits wide
  assign or_16_out = and_80_out | or_17_out;  // OR_Gate or_16, 15 bits wide
  assign or_17_out = and_81_out | or_18_out;  // OR_Gate or_17, 15 bits wide
  assign or_18_out = and_82_out | or_19_out;  // OR_Gate or_18, 15 bits wide
  assign or_19_out = and_83_out | or_20_out;  // OR_Gate or_19, 15 bits wide
  assign or_20_out = and_84_out | or_21_out;  // OR_Gate or_20, 15 bits wide
  assign or_21_out = and_85_out | or_22_out;  // OR_Gate or_21, 15 bits wide
  assign or_22_out = and_86_out | or_23_out;  // OR_Gate or_22, 15 bits wide
  assign or_23_out = and_87_out | or_24_out;  // OR_Gate or_23, 15 bits wide
  assign or_24_out = and_88_out | or_25_out;  // OR_Gate or_24, 15 bits wide
  assign or_25_out = and_89_out | or_26_out;  // OR_Gate or_25, 15 bits wide
  assign or_26_out = and_90_out | or_27_out;  // OR_Gate or_26, 15 bits wide
  assign or_27_out = and_91_out | or_28_out;  // OR_Gate or_27, 15 bits wide
  assign or_28_out = and_92_out | or_29_out;  // OR_Gate or_28, 15 bits wide
  assign or_29_out = and_93_out | or_30_out;  // OR_Gate or_29, 15 bits wide
  assign or_30_out = and_94_out | or_31_out;  // OR_Gate or_30, 15 bits wide
  assign or_31_out = and_95_out | or_32_out;  // OR_Gate or_31, 15 bits wide
  assign or_32_out = and_96_out | or_33_out;  // OR_Gate or_32, 15 bits wide
  assign or_33_out = and_97_out | or_34_out;  // OR_Gate or_33, 15 bits wide
  assign or_34_out = and_98_out | or_35_out;  // OR_Gate or_34, 15 bits wide
  assign or_35_out = and_99_out | or_36_out;  // OR_Gate or_35, 15 bits wide
  assign or_36_out = and_100_out | or_37_out;  // OR_Gate or_36, 15 bits wide
  assign or_37_out = and_101_out | or_38_out;  // OR_Gate or_37, 15 bits wide
  assign or_38_out = and_102_out | or_39_out;  // OR_Gate or_38, 15 bits wide
  assign or_39_out = and_103_out | or_40_out;  // OR_Gate or_39, 15 bits wide
  assign or_40_out = and_104_out | or_41_out;  // OR_Gate or_40, 15 bits wide
  assign or_41_out = and_105_out | or_42_out;  // OR_Gate or_41, 15 bits wide
  assign or_42_out = and_106_out | or_43_out;  // OR_Gate or_42, 15 bits wide
  assign or_43_out = and_107_out | or_44_out;  // OR_Gate or_43, 15 bits wide
  assign or_44_out = and_108_out | or_45_out;  // OR_Gate or_44, 15 bits wide
  assign or_45_out = and_109_out | or_46_out;  // OR_Gate or_45, 15 bits wide
  assign or_46_out = and_110_out | or_47_out;  // OR_Gate or_46, 15 bits wide
  assign or_47_out = and_111_out | or_48_out;  // OR_Gate or_47, 15 bits wide
  assign or_48_out = and_112_out | or_49_out;  // OR_Gate or_48, 15 bits wide
  assign or_49_out = and_113_out | or_50_out;  // OR_Gate or_49, 15 bits wide
  assign or_50_out = and_114_out | or_51_out;  // OR_Gate or_50, 15 bits wide
  assign or_51_out = and_115_out | or_52_out;  // OR_Gate or_51, 15 bits wide
  assign or_52_out = and_116_out | or_53_out;  // OR_Gate or_52, 15 bits wide
  assign or_53_out = and_117_out | or_54_out;  // OR_Gate or_53, 15 bits wide
  assign or_54_out = and_118_out | or_55_out;  // OR_Gate or_54, 15 bits wide
  assign or_55_out = and_119_out | or_56_out;  // OR_Gate or_55, 15 bits wide
  assign or_56_out = and_120_out | or_57_out;  // OR_Gate or_56, 15 bits wide
  assign or_57_out = and_121_out | or_58_out;  // OR_Gate or_57, 15 bits wide
  assign or_58_out = and_122_out | or_59_out;  // OR_Gate or_58, 15 bits wide
  assign or_59_out = and_123_out | or_60_out;  // OR_Gate or_59, 15 bits wide
  assign or_60_out = and_124_out | or_61_out;  // OR_Gate or_60, 15 bits wide
  assign or_61_out = and_125_out | or_62_out;  // OR_Gate or_61, 15 bits wide
  assign or_62_out = and_126_out | or_63_out;  // OR_Gate or_62, 15 bits wide
  assign or_63_out = and_127_out | or_64_out;  // OR_Gate or_63, 15 bits wide
  assign or_64_out = and_128_out | {15{1'b0}};  // OR_Gate or_64, 15 bits wide

  // Notes on the sheet:
  //   OP: 0
  //   OP: 1
  //   OP: 2
  //   OP: 3
  //   OP: 4
  //   OP: 5
  //   OP: 6
  //   OP: 7
  //   OP: 8
  //   OP: 9
  //   OP: 10
  //   OP: 11
  //   OP: 12
  //   OP: 13
  //   OP: 14
  //   OP: 15
  //   OP: 16
  //   OP: 17
  //   OP: 18
  //   OP: 19
  //   OP: 20
  //   OP: 21
  //   OP: 22
  //   OP: 23
  //   OP: 24
  //   OP: 25
  //   OP: 26
  //   OP: 27
  //   OP: 28
  //   OP: 29
  //   OP: 30
  //   OP: 31
  //   OP: 32
  //   OP: 33
  //   OP: 34
  //   OP: 35
  //   OP: 36
  //   OP: 37
  //   OP: 38
  //   OP: 39
  //   OP: 40
  //   OP: 41
  //   OP: 42
  //   OP: 43
  //   OP: 44
  //   OP: 45
  //   OP: 46
  //   OP: 47
  //   OP: 48
  //   OP: 49
  //   OP: 50
  //   OP: 51
  //   OP: 52
  //   OP: 53
  //   OP: 54
  //   OP: 55
  //   OP: 56
  //   OP: 57
  //   OP: 58
  //   OP: 59
  //   OP: 60
  //   OP: 61
  //   OP: 62
  //   OP: 63
  //   R-Type
  //   j
  //   jal
  //   beq
  //   bne
  //   blez
  //   bgtz
  //   addi
  //   addiu
  //   slti
  //   sltiu
  //   andi
  //   ori
  //   xori
  //   lui
  //   F-Type
  //   lb
  //   lh
  //   lwl
  //   lw
  //   lbu
  //   lhu
  //   lwr
  //   sb
  //   sh
  //   swl
  //   sw
  //   swr
  //   cache
  //   ll
  //   lwc1
  //   lwc2
  //   pref
  //   ldc1
  //   ldc2
  //   sc
  //   swc1
  //   swc2
  //   sdc1
  //   sdc2
  //   1-00-0000-0-1000-00-1
  //   not yet implemented
  //   not yet implemented
  //   0-00-0000-1-0010-00-0
  //   not yet implemented
  //   not yet implemented
  //   not yet implemented
  //   1-00-0000-0-0000-01-0
  //   1-00-0000-0-0001-10-0
  //   1-00-0000-0-0011-01-0
  //   1-00-0000-0-0100-01-0
  //   1-00-0000-0-0101-01-0
  //   1-00-0000-0-0110-01-0
  //   1-00-0000-0-0111-01-0
  //   1-10-0000-0-0000-00-0
  //   not yet implemented
  //   1-01-0000-0-0000-01-0
  //   1-01-0001-0-0000-01-0
  //   1-01-0110-0-0000-01-0
  //   1-01-0010-0-0000-01-0
  //   1-01-0100-0-0000-01-0
  //   1-01-0101-0-0000-01-0
  //   1-01-0111-0-0000-01-0
  //   0-00-1000-0-0000-01-0
  //   0-00-1001-0-0000-01-0
  //   0-00-1110-0-0000-01-0
  //   0-00-1010-0-0000-01-0
  //   0-00-1111-0-0000-01-0
  //   not yet implemented
  //   not yet implemented
  //   not yet implemented
  //   not yet implemented
  //   not yet implemented
  //   not yet implemented
  //   not yet implemented
  //   not yet implemented
  //   not yet implemented
  //   not yet implemented
  //   not yet implemented
  //   not yet implemented
  //   MemOp Codes:
  //   0000 - lb
  //   0001 - lh
  //   0010 - lw
  //   0011 - N/A
  //   0100 - lbu
  //   0101 - lhu
  //   0110 - lwl
  //   0111 - lwr
  //   ALUOp Codes:
  //   0000 - add
  //   0001 - addu
  //   0010 - subu
  //   0011 - slt
  //   0100 - sltu
  //   0101 - and
  //   0110 - or
  //   0111 - xor
  //   1XXX - Look at value of Func
  //   1000 - sb
  //   1001 - sh
  //   1010 - sw
  //   1011 - N/A
  //   1100 - N/A
  //   1101 - N/A
  //   1110 - swl
  //   1111 - swr
  //   TODO: Restore proper functionality to addiu in which immediate value is sign extended rather than zero extended and lui output is data forwarded
endmodule

module ALUDecoder (
  input  [3:0] ALUOp,
  input  [5:0] Func,
  output NOT_ALUOut,
  output [3:0] ALUControl
);

  wire and_1_out, and_2_out, and_3_out, and_4_out, and_5_out, and_6_out, and_7_out, and_8_out, and_9_out,
       and_10_out, and_11_out, and_12_out, and_13_out, and_14_out, and_15_out, and_16_out, and_17_out,
       and_18_out, and_19_out, and_20_out, and_21_out, and_22_out, and_23_out, and_24_out, or_1_out,
       or_2_out, or_3_out, or_4_out, or_5_out, or_6_out, or_7_out, or_8_out, or_9_out, or_10_out, or_11_out,
       or_12_out, or_13_out, or_14_out, or_15_out, or_16_out;
  wire [3:0] and_25_out, and_26_out, and_27_out, and_28_out, and_29_out, and_30_out, and_31_out, and_32_out,
       and_33_out, and_34_out, and_35_out, and_36_out, and_37_out, and_38_out, and_39_out, and_40_out,
       bit_extender_1_out, bit_extender_2_out, bit_extender_3_out, bit_extender_4_out, bit_extender_5_out,
       bit_extender_6_out, bit_extender_7_out, bit_extender_8_out, bit_extender_9_out, bit_extender_10_out,
       bit_extender_11_out, bit_extender_12_out, bit_extender_13_out, bit_extender_14_out,
       bit_extender_15_out, bit_extender_16_out, or_18_out, or_19_out, or_20_out, or_21_out, or_22_out,
       or_23_out, or_24_out, or_25_out, or_26_out, or_27_out, or_28_out, or_29_out, or_30_out, or_31_out,
       or_32_out;

  and and_1 (and_1_out, ~ALUOp[3], ALUOp[2], ~ALUOp[1], ALUOp[0]);  // AND_Gate
  and and_2 (and_2_out, Func[5], ~Func[4], ~Func[3], Func[2], ~Func[1], ~Func[0], ALUOp[3]);  // AND_Gate
  and and_3 (and_3_out, ~ALUOp[3], ALUOp[2], ALUOp[1], ~ALUOp[0]);  // AND_Gate
  and and_4 (and_4_out, Func[5], ~Func[4], ~Func[3], Func[2], ~Func[1], ~Func[0], ALUOp[3]);  // AND_Gate
  and and_5 (and_5_out, ~ALUOp[3], ALUOp[2], ALUOp[1], ALUOp[0]);  // AND_Gate
  and and_6 (and_6_out, Func[5], ~Func[4], ~Func[3], ~Func[2], ~Func[1], ~Func[0], ALUOp[3]);  // AND_Gate
  and and_7 (and_7_out, ~Func[5], ~Func[4], ~Func[3], ~Func[2], ~Func[1], ~Func[0], ALUOp[3]);  // AND_Gate
  and and_8 (and_8_out, ~Func[5], ~Func[4], ~Func[3], ~Func[2], Func[1], ~Func[0], ALUOp[3]);  // AND_Gate
  and and_9 (and_9_out, ~Func[5], ~Func[4], ~Func[3], ~Func[2], Func[1], Func[0], ALUOp[3]);  // AND_Gate
  and and_10 (and_10_out, ~ALUOp[3], ~ALUOp[2], ~ALUOp[1], ~ALUOp[0]);  // AND_Gate
  and and_11 (and_11_out, Func[5], ~Func[4], ~Func[3], ~Func[2], ~Func[1], ~Func[0], ALUOp[3]);  // AND_Gate
  and and_12 (and_12_out, ~ALUOp[3], ~ALUOp[2], ~ALUOp[1], ALUOp[0]);  // AND_Gate
  and and_13 (and_13_out, Func[5], ~Func[4], ~Func[3], ~Func[2], ~Func[1], Func[0], ALUOp[3]);  // AND_Gate
  and and_14 (and_14_out, Func[5], ~Func[4], ~Func[3], ~Func[2], Func[1], ~Func[0], ALUOp[3]);  // AND_Gate
  and and_15 (and_15_out, ~ALUOp[3], ~ALUOp[2], ALUOp[1], ~ALUOp[0]);  // AND_Gate
  and and_16 (and_16_out, Func[5], ~Func[4], ~Func[3], ~Func[2], Func[1], Func[0], ALUOp[3]);  // AND_Gate
  and and_17 (and_17_out, ~Func[5], Func[4], Func[3], ~Func[2], ~Func[1], ~Func[0], ALUOp[3]);  // AND_Gate
  and and_18 (and_18_out, ~Func[5], Func[4], Func[3], ~Func[2], ~Func[1], Func[0], ALUOp[3]);  // AND_Gate
  and and_19 (and_19_out, ~Func[5], Func[4], Func[3], ~Func[2], Func[1], ~Func[0], ALUOp[3]);  // AND_Gate
  and and_20 (and_20_out, ~Func[5], Func[4], Func[3], ~Func[2], Func[1], Func[0], ALUOp[3]);  // AND_Gate
  and and_21 (and_21_out, ~ALUOp[3], ~ALUOp[2], ALUOp[1], ALUOp[0]);  // AND_Gate
  and and_22 (and_22_out, Func[5], ~Func[4], Func[3], ~Func[2], Func[1], ~Func[0], ALUOp[3]);  // AND_Gate
  and and_23 (and_23_out, ~ALUOp[3], ALUOp[2], ~ALUOp[1], ~ALUOp[0]);  // AND_Gate
  and and_24 (and_24_out, Func[5], ~Func[4], Func[3], ~Func[2], Func[1], Func[0], ALUOp[3]);  // AND_Gate
  or or_1 (or_1_out, and_1_out, and_2_out);
  or or_2 (or_2_out, and_3_out, and_4_out);
  or or_3 (or_3_out, and_5_out, and_6_out);
  buf or_4 (or_4_out, and_7_out);  // OR_Gate
  buf or_5 (or_5_out, and_8_out);  // OR_Gate
  buf or_6 (or_6_out, and_9_out);  // OR_Gate
  or or_7 (or_7_out, and_10_out, and_11_out);
  or or_8 (or_8_out, and_12_out, and_13_out);
  buf or_9 (or_9_out, and_14_out);  // OR_Gate
  or or_10 (or_10_out, and_15_out, and_16_out);
  buf or_11 (or_11_out, and_17_out);  // OR_Gate
  buf or_12 (or_12_out, and_18_out);  // OR_Gate
  buf or_13 (or_13_out, and_19_out);  // OR_Gate
  buf or_14 (or_14_out, and_20_out);  // OR_Gate
  or or_15 (or_15_out, and_21_out, and_22_out);
  or or_16 (or_16_out, and_23_out, and_24_out);
  assign bit_extender_1_out = {{3{or_1_out}}, or_1_out};  // Bit_Extender bit_extender_1
  assign bit_extender_2_out = {{3{or_2_out}}, or_2_out};  // Bit_Extender bit_extender_2
  assign bit_extender_3_out = {{3{or_3_out}}, or_3_out};  // Bit_Extender bit_extender_3
  assign bit_extender_4_out = {{3{or_4_out}}, or_4_out};  // Bit_Extender bit_extender_4
  assign bit_extender_5_out = {{3{or_5_out}}, or_5_out};  // Bit_Extender bit_extender_5
  assign bit_extender_6_out = {{3{or_6_out}}, or_6_out};  // Bit_Extender bit_extender_6
  assign bit_extender_7_out = {{3{or_7_out}}, or_7_out};  // Bit_Extender bit_extender_7
  assign bit_extender_8_out = {{3{or_8_out}}, or_8_out};  // Bit_Extender bit_extender_8
  assign bit_extender_9_out = {{3{or_9_out}}, or_9_out};  // Bit_Extender bit_extender_9
  assign bit_extender_10_out = {{3{or_10_out}}, or_10_out};  // Bit_Extender bit_extender_10
  assign bit_extender_11_out = {{3{or_11_out}}, or_11_out};  // Bit_Extender bit_extender_11
  assign bit_extender_12_out = {{3{or_12_out}}, or_12_out};  // Bit_Extender bit_extender_12
  assign bit_extender_13_out = {{3{or_13_out}}, or_13_out};  // Bit_Extender bit_extender_13
  assign bit_extender_14_out = {{3{or_14_out}}, or_14_out};  // Bit_Extender bit_extender_14
  assign bit_extender_15_out = {{3{or_15_out}}, or_15_out};  // Bit_Extender bit_extender_15
  assign bit_extender_16_out = {{3{or_16_out}}, or_16_out};  // Bit_Extender bit_extender_16
  assign and_25_out = 4'b0000 & bit_extender_1_out;  // AND_Gate and_25, 4 bits wide
  assign and_26_out = 4'b0001 & bit_extender_2_out;  // AND_Gate and_26, 4 bits wide
  assign and_27_out = 4'b0010 & bit_extender_3_out;  // AND_Gate and_27, 4 bits wide
  assign and_28_out = 4'b0011 & bit_extender_4_out;  // AND_Gate and_28, 4 bits wide
  assign and_29_out = 4'b0100 & bit_extender_5_out;  // AND_Gate and_29, 4 bits wide
  assign and_30_out = 4'b0101 & bit_extender_6_out;  // AND_Gate and_30, 4 bits wide
  assign and_31_out = 4'b0110 & bit_extender_7_out;  // AND_Gate and_31, 4 bits wide
  assign and_32_out = 4'b0111 & bit_extender_8_out;  // AND_Gate and_32, 4 bits wide
  assign and_33_out = 4'b1000 & bit_extender_9_out;  // AND_Gate and_33, 4 bits wide
  assign and_34_out = 4'b1001 & bit_extender_10_out;  // AND_Gate and_34, 4 bits wide
  assign and_35_out = 4'b1010 & bit_extender_11_out;  // AND_Gate and_35, 4 bits wide
  assign and_36_out = 4'b1011 & bit_extender_12_out;  // AND_Gate and_36, 4 bits wide
  assign and_37_out = 4'b1100 & bit_extender_13_out;  // AND_Gate and_37, 4 bits wide
  assign and_38_out = 4'b1101 & bit_extender_14_out;  // AND_Gate and_38, 4 bits wide
  assign and_39_out = 4'b1110 & bit_extender_15_out;  // AND_Gate and_39, 4 bits wide
  assign and_40_out = 4'b1111 & bit_extender_16_out;  // AND_Gate and_40, 4 bits wide
  assign ALUControl = and_25_out | or_18_out;  // OR_Gate or_17, 4 bits wide
  assign or_18_out = and_26_out | or_19_out;  // OR_Gate or_18, 4 bits wide
  assign or_19_out = and_27_out | or_20_out;  // OR_Gate or_19, 4 bits wide
  assign or_20_out = and_28_out | or_21_out;  // OR_Gate or_20, 4 bits wide
  assign or_21_out = and_29_out | or_22_out;  // OR_Gate or_21, 4 bits wide
  assign or_22_out = and_30_out | or_23_out;  // OR_Gate or_22, 4 bits wide
  assign or_23_out = and_31_out | or_24_out;  // OR_Gate or_23, 4 bits wide
  assign or_24_out = and_32_out | or_25_out;  // OR_Gate or_24, 4 bits wide
  assign or_25_out = and_33_out | or_26_out;  // OR_Gate or_25, 4 bits wide
  assign or_26_out = and_34_out | or_27_out;  // OR_Gate or_26, 4 bits wide
  assign or_27_out = and_35_out | or_28_out;  // OR_Gate or_27, 4 bits wide
  assign or_28_out = and_36_out | or_29_out;  // OR_Gate or_28, 4 bits wide
  assign or_29_out = and_37_out | or_30_out;  // OR_Gate or_29, 4 bits wide
  assign or_30_out = and_38_out | or_31_out;  // OR_Gate or_30, 4 bits wide
  assign or_31_out = and_39_out | or_32_out;  // OR_Gate or_31, 4 bits wide
  assign or_32_out = and_40_out | 4'b0000;  // OR_Gate or_32, 4 bits wide

  assign NOT_ALUOut = 1'b0;

  // Notes on the sheet:
  //   andi
  //   and
  //   ori
  //   or
  //   xori
  //   xor
  //   TODO: Add nor/nand/etc functionality
  //   0000 - A & B
  //   0001 - A | B
  //   0010 - A ^ B
  //   0110 - A + B
  //   1000 - A - B
  //   1010 - A * B
  //   1100 - A / B
  //   1110 - slt Q, A, B
  //   1111 - sltu Q, A, B
  //   0011 - A<<B (logical)
  //   0100 - A >> B (logical)
  //   0101 - A >> B (arith.)
  //   0111 - A + B (unsigned)
  //   1001 - A - B (unsigned)
  //   1011 - A * B (unsigned)
  //   1101 - A / B (unsigned)
  //   ALUOp Codes:
  //   0000 - add
  //   0001 - addu
  //   0010 - subu
  //   0011 - slt
  //   0100 - sltu
  //   0101 - and
  //   0110 - or
  //   0111 - xor
  //   ALUControl Codes:
  //   0000 - A & B
  //   0001 - A | B
  //   0010 - A ^ B
  //   0110 - A + B
  //   1000 - A - B
  //   1010 - A * B
  //   1100 - A / B
  //   1110 - slt Q, A, B
  //   1XXX - Look at value of Func
  //   0011 - A << B (logical)
  //   0100 - A >> B (logical)
  //   0101 - A >> B (arith.)
  //   0111 - A + B (unsigned)
  //   1001 - A - B (unsigned)
  //   1011 - A * B (unsigned)
  //   1101 - A / B (unsigned)
  //   1111 - sltu Q, A, B
endmodule

module RegisterFile (
  input  [4:0] Address1,
  input  [4:0] Address2,
  input  WriteEnable3,
  input  [4:0] Address3,
  input  [31:0] WriteData3,
  input  CLK,
  input  Reset,
  output [31:0] RegisterData1,
  output [31:0] RegisterData2
);

  wire demultiplexer_1_out0, demultiplexer_1_out1, demultiplexer_1_out2, demultiplexer_1_out3,
       demultiplexer_1_out4, demultiplexer_1_out5, demultiplexer_1_out6, demultiplexer_1_out7,
       demultiplexer_1_out8, demultiplexer_1_out9, demultiplexer_1_out10, demultiplexer_1_out11,
       demultiplexer_1_out12, demultiplexer_1_out13, demultiplexer_1_out14, demultiplexer_1_out15,
       demultiplexer_1_out16, demultiplexer_1_out17, demultiplexer_1_out18, demultiplexer_1_out19,
       demultiplexer_1_out20, demultiplexer_1_out21, demultiplexer_1_out22, demultiplexer_1_out23,
       demultiplexer_1_out24, demultiplexer_1_out25, demultiplexer_1_out26, demultiplexer_1_out27,
       demultiplexer_1_out28, demultiplexer_1_out29, demultiplexer_1_out30, demultiplexer_1_out31, or_1_out,
       or_2_out, or_3_out;
  wire [31:0] multiplexer_2_out, multiplexer_3_out, multiplexer_4_out, r00_0_q, r0a_t2_q, r0b_t3_q, r0c_t4_q,
       r0d_t5_q, r0e_t6_q, r0f_t7_q, r01_at_q, r1a_k0_q, r1b_k1_q, r1c_gp_q, r1d_sp_q, r1e_fp_q, r1f_ra_q,
       r02_v0_q, r03_v1_q, r04_a0_q, r05_a1_q, r06_a2_q, r07_a3_q, r08_t0_q, r09_t1_q, r10_s0_q, r11_s1_q,
       r12_s2_q, r13_s3_q, r14_s4_q, r15_s5_q, r16_s6_q, r17_s7_q, r18_t8_q, r19_t9_q;

  Demultiplexer #(.select(5)) demultiplexer_1 (
    .out0(demultiplexer_1_out0), .out1(demultiplexer_1_out1), .out2(demultiplexer_1_out2),
    .out3(demultiplexer_1_out3), .out4(demultiplexer_1_out4), .out5(demultiplexer_1_out5),
    .out6(demultiplexer_1_out6), .out7(demultiplexer_1_out7), .out8(demultiplexer_1_out8),
    .out9(demultiplexer_1_out9), .out10(demultiplexer_1_out10), .out11(demultiplexer_1_out11),
    .out12(demultiplexer_1_out12), .out13(demultiplexer_1_out13), .out14(demultiplexer_1_out14),
    .out15(demultiplexer_1_out15), .out16(demultiplexer_1_out16), .out17(demultiplexer_1_out17),
    .out18(demultiplexer_1_out18), .out19(demultiplexer_1_out19), .out20(demultiplexer_1_out20),
    .out21(demultiplexer_1_out21), .out22(demultiplexer_1_out22), .out23(demultiplexer_1_out23),
    .out24(demultiplexer_1_out24), .out25(demultiplexer_1_out25), .out26(demultiplexer_1_out26),
    .out27(demultiplexer_1_out27), .out28(demultiplexer_1_out28), .out29(demultiplexer_1_out29),
    .out30(demultiplexer_1_out30), .out31(demultiplexer_1_out31), .in(WriteEnable3), .sel(Address3));
  Register #(.trigger("falling"), .width(32)) r00_0 (
    .D({32{1'b0}}), .en(demultiplexer_1_out0), .clk(CLK), .Q(r00_0_q));  // open: clr
  Register #(.trigger("falling"), .width(32)) r01_at (
    .D(WriteData3), .en(demultiplexer_1_out1), .clk(CLK), .Q(r01_at_q), .clr(Reset));
  Register #(.trigger("falling"), .width(32)) r02_v0 (
    .D(WriteData3), .en(demultiplexer_1_out2), .clk(CLK), .Q(r02_v0_q), .clr(Reset));
  Register #(.trigger("falling"), .width(32)) r03_v1 (
    .D(WriteData3), .en(demultiplexer_1_out3), .clk(CLK), .Q(r03_v1_q), .clr(Reset));
  Register #(.trigger("falling"), .width(32)) r04_a0 (
    .D(WriteData3), .en(demultiplexer_1_out4), .clk(CLK), .Q(r04_a0_q), .clr(Reset));
  Register #(.trigger("falling"), .width(32)) r05_a1 (
    .D(WriteData3), .en(demultiplexer_1_out5), .clk(CLK), .Q(r05_a1_q), .clr(Reset));
  Register #(.trigger("falling"), .width(32)) r06_a2 (
    .D(WriteData3), .en(demultiplexer_1_out6), .clk(CLK), .Q(r06_a2_q), .clr(Reset));
  Register #(.trigger("falling"), .width(32)) r07_a3 (
    .D(WriteData3), .en(demultiplexer_1_out7), .clk(CLK), .Q(r07_a3_q), .clr(Reset));
  Register #(.trigger("falling"), .width(32)) r08_t0 (
    .D(WriteData3), .en(demultiplexer_1_out8), .clk(CLK), .Q(r08_t0_q), .clr(Reset));
  Register #(.trigger("falling"), .width(32)) r09_t1 (
    .D(WriteData3), .en(demultiplexer_1_out9), .clk(CLK), .Q(r09_t1_q), .clr(Reset));
  Register #(.trigger("falling"), .width(32)) r0a_t2 (
    .D(WriteData3), .en(demultiplexer_1_out10), .clk(CLK), .Q(r0a_t2_q), .clr(Reset));
  Register #(.trigger("falling"), .width(32)) r0b_t3 (
    .D(WriteData3), .en(demultiplexer_1_out11), .clk(CLK), .Q(r0b_t3_q), .clr(Reset));
  Register #(.trigger("falling"), .width(32)) r0c_t4 (
    .D(WriteData3), .en(demultiplexer_1_out12), .clk(CLK), .Q(r0c_t4_q), .clr(Reset));
  Register #(.trigger("falling"), .width(32)) r0d_t5 (
    .D(WriteData3), .en(demultiplexer_1_out13), .clk(CLK), .Q(r0d_t5_q), .clr(Reset));
  Register #(.trigger("falling"), .width(32)) r0e_t6 (
    .D(WriteData3), .en(demultiplexer_1_out14), .clk(CLK), .Q(r0e_t6_q), .clr(Reset));
  Register #(.trigger("falling"), .width(32)) r0f_t7 (
    .D(WriteData3), .en(demultiplexer_1_out15), .clk(CLK), .Q(r0f_t7_q), .clr(Reset));
  Register #(.trigger("falling"), .width(32)) r10_s0 (
    .D(WriteData3), .en(demultiplexer_1_out16), .clk(CLK), .Q(r10_s0_q), .clr(Reset));
  Register #(.trigger("falling"), .width(32)) r11_s1 (
    .D(WriteData3), .en(demultiplexer_1_out17), .clk(CLK), .Q(r11_s1_q), .clr(Reset));
  Register #(.trigger("falling"), .width(32)) r12_s2 (
    .D(WriteData3), .en(demultiplexer_1_out18), .clk(CLK), .Q(r12_s2_q), .clr(Reset));
  Register #(.trigger("falling"), .width(32)) r13_s3 (
    .D(WriteData3), .en(demultiplexer_1_out19), .clk(CLK), .Q(r13_s3_q), .clr(Reset));
  Register #(.trigger("falling"), .width(32)) r14_s4 (
    .D(WriteData3), .en(demultiplexer_1_out20), .clk(CLK), .Q(r14_s4_q), .clr(Reset));
  Register #(.trigger("falling"), .width(32)) r15_s5 (
    .D(WriteData3), .en(demultiplexer_1_out21), .clk(CLK), .Q(r15_s5_q), .clr(Reset));
  Register #(.trigger("falling"), .width(32)) r16_s6 (
    .D(WriteData3), .en(demultiplexer_1_out22), .clk(CLK), .Q(r16_s6_q), .clr(Reset));
  Register #(.trigger("falling"), .width(32)) r17_s7 (
    .D(WriteData3), .en(demultiplexer_1_out23), .clk(CLK), .Q(r17_s7_q), .clr(Reset));
  Multiplexer #(.select(5), .width(32)) multiplexer_1 (
    .in0(r00_0_q), .in1(r01_at_q), .in2(r02_v0_q), .in3(r03_v1_q), .in4(r04_a0_q), .in5(r05_a1_q),
    .in6(r06_a2_q), .in7(r07_a3_q), .in8(r08_t0_q), .in9(r09_t1_q), .in10(r0a_t2_q), .in11(r0b_t3_q),
    .in12(r0c_t4_q), .in13(r0d_t5_q), .in14(r0e_t6_q), .in15(r0f_t7_q), .in16(r10_s0_q), .in17(r11_s1_q),
    .in18(r12_s2_q), .in19(r13_s3_q), .in20(r14_s4_q), .in21(r15_s5_q), .in22(r16_s6_q), .in23(r17_s7_q),
    .in24(r18_t8_q), .in25(r19_t9_q), .in26(r1a_k0_q), .in27(r1b_k1_q), .in28(r1c_gp_q), .in29(r1d_sp_q),
    .in30(r1e_fp_q), .in31(r1f_ra_q), .out(RegisterData1), .sel(Address1));
  Register #(.trigger("falling"), .width(32)) r18_t8 (
    .D(WriteData3), .en(demultiplexer_1_out24), .clk(CLK), .Q(r18_t8_q), .clr(Reset));
  Register #(.trigger("falling"), .width(32)) r19_t9 (
    .D(WriteData3), .en(demultiplexer_1_out25), .clk(CLK), .Q(r19_t9_q), .clr(Reset));
  Register #(.trigger("falling"), .width(32)) r1a_k0 (
    .D(WriteData3), .en(demultiplexer_1_out26), .clk(CLK), .Q(r1a_k0_q), .clr(Reset));
  Register #(.trigger("falling"), .width(32)) r1b_k1 (
    .D(WriteData3), .en(demultiplexer_1_out27), .clk(CLK), .Q(r1b_k1_q), .clr(Reset));
  Register #(.trigger("falling"), .width(32)) r1c_gp (
    .D(multiplexer_2_out), .en(or_1_out), .clk(CLK), .Q(r1c_gp_q));  // open: clr
  Multiplexer #(.width(32)) multiplexer_2 (.in0(WriteData3), .in1(32'h7f000000), .out(multiplexer_2_out), .sel(Reset));
  or or_1 (or_1_out, demultiplexer_1_out28, Reset);
  Register #(.trigger("falling"), .width(32)) r1d_sp (
    .D(multiplexer_3_out), .en(or_2_out), .clk(CLK), .Q(r1d_sp_q));  // open: clr
  Multiplexer #(.width(32)) multiplexer_3 (.in0(WriteData3), .in1(32'h80000000), .out(multiplexer_3_out), .sel(Reset));
  or or_2 (or_2_out, demultiplexer_1_out29, Reset);
  Register #(.trigger("falling"), .width(32)) r1e_fp (
    .D(multiplexer_4_out), .en(or_3_out), .clk(CLK), .Q(r1e_fp_q));  // open: clr
  Multiplexer #(.width(32)) multiplexer_4 (.in0(WriteData3), .in1(32'h80000000), .out(multiplexer_4_out), .sel(Reset));
  or or_3 (or_3_out, demultiplexer_1_out30, Reset);
  Register #(.trigger("falling"), .width(32)) r1f_ra (
    .D(WriteData3), .en(demultiplexer_1_out31), .clk(CLK), .Q(r1f_ra_q), .clr(Reset));
  Multiplexer #(.select(5), .width(32)) multiplexer_5 (
    .in0(r00_0_q), .in1(r01_at_q), .in2(r02_v0_q), .in3(r03_v1_q), .in4(r04_a0_q), .in5(r05_a1_q),
    .in6(r06_a2_q), .in7(r07_a3_q), .in8(r08_t0_q), .in9(r09_t1_q), .in10(r0a_t2_q), .in11(r0b_t3_q),
    .in12(r0c_t4_q), .in13(r0d_t5_q), .in14(r0e_t6_q), .in15(r0f_t7_q), .in16(r10_s0_q), .in17(r11_s1_q),
    .in18(r12_s2_q), .in19(r13_s3_q), .in20(r14_s4_q), .in21(r15_s5_q), .in22(r16_s6_q), .in23(r17_s7_q),
    .in24(r18_t8_q), .in25(r19_t9_q), .in26(r1a_k0_q), .in27(r1b_k1_q), .in28(r1c_gp_q), .in29(r1d_sp_q),
    .in30(r1e_fp_q), .in31(r1f_ra_q), .out(RegisterData2), .sel(Address2));

  // Notes on the sheet:
  //   Write Data 3 goes to all
  //   Register File
  //   Registers addressed 0-31
  //   32-bit registers
  //   Write on falling clock edge,
  //   read is async
  //   Write Functionality
  //   Reading Functionality
  //   0
  //   32
  //   Outputs of Registers
endmodule

module MainMemory (
  input  [31:0] Address,
  input  [31:0] DataIn,
  input  [3:0] MemOp,
  input  CLK,
  output AdES_AddressErrorException,
  output [31:0] DataOut
);

  wire priority_encoder_1_out;
  wire [1:0] datasection_1_invalidaddressflag, not_1_out;
  wire [31:0] datasection_1_dataout, multiplexer_1_out, stacksection_1_dataout;

  DataSection datasection_1 (
    .MemOp(MemOp), .Address(Address), .DataIn(DataIn), .CLK(CLK), .DataOut(datasection_1_dataout),
    .InvalidAddressFlag(datasection_1_invalidaddressflag[0]));
  StackSection stacksection_1 (
    .MemOp(MemOp), .Address(Address), .DataIn(DataIn), .CLK(CLK), .DataOut(stacksection_1_dataout),
    .InvalidAddressFlag(datasection_1_invalidaddressflag[1]));
  assign not_1_out = ~datasection_1_invalidaddressflag;  // NOT_Gate not_1, 2 bits wide
  Priority_Encoder #(.select(1)) priority_encoder_1 (
    .in0(not_1_out[0]), .in1(not_1_out[1]), .out(priority_encoder_1_out), .en_out(AdES_AddressErrorException));  // open: gs, en_in
  Multiplexer #(.width(32)) multiplexer_1 (
    .in0(datasection_1_dataout), .in1(stacksection_1_dataout), .out(multiplexer_1_out),
    .sel(priority_encoder_1_out));
  Multiplexer #(.width(32)) multiplexer_2 (
    .in0(multiplexer_1_out), .in1({32{1'b0}}), .out(DataOut), .sel(AdES_AddressErrorException));

  // Notes on the sheet:
  //   Outputs 0x0 when address is invalid
  //   InvalidAddress = 1 when a seg. fault occurs
  //   or invalid address alignment
  //   MemOp Codes:
  //   0000 - lb
  //   0001 - lh
  //   0010 - lw
  //   0100 - lbu
  //   0101 - lhu
  //   0110 - lwl
  //   0111 - lwr
  //   0011 - N/A
  //   1000 - sb
  //   1001 - sh
  //   1010 - sw
  //   1011 - N/A
  //   1100 - N/A
  //   1101 - N/A
  //   1110 - swl
  //   1111 - swr
endmodule

module TextSection (
  input  [31:0] Address,
  output [31:0] Instruction,
  output InvalidAddressFlag
);

  wire subtractor_1_bout;
  wire [31:0] subtractor_1_out;

  Subtractor #(.width(32)) subtractor_1 (
    .a(Address), .b(32'h400000), .out(subtractor_1_out), .bout(subtractor_1_bout));  // open: bin
  or or_1 (InvalidAddressFlag, subtractor_1_bout, subtractor_1_out[31], subtractor_1_out[30], subtractor_1_out[29], subtractor_1_out[28], subtractor_1_out[27], subtractor_1_out[26], subtractor_1_out[1], subtractor_1_out[0]);
  ROM #(.addrWidth(24), .dataWidth(32)) text_section (
    .addr(subtractor_1_out[25:2]),
    .data({Instruction[7:0], Instruction[15:8], Instruction[23:16], Instruction[31:24]}));

  // Notes on the sheet:
  //   Instruction Memory Range:
  //   0x0040 0000 - 0x043f ffff
  //   contents of text_section (hex, n*v repeats v):
  //   10103c 1026 1124 0 0 5000292a 0 0 c002011 0 0 20401102 0 83901100 0 0 12ad 4003122 f2ff0010 0 0
  //   ecffbd23
  //   <<=======
  //   <<=======
  //   LOAD bin/text FILE HERE!
  //   RIGHT CLICK RAM:
  //   Load Image > bin/data
  //   **Leave it decoding in Big-Endian**
endmodule

module RODataSection (
  input  IsReadingByte,
  input  [31:0] Address,
  output [31:0] Data,
  output InvalidAddressFlag
);

  wire and_1_out, or_1_out, subtractor_1_bout;
  wire [7:0] multiplexer_1_out;
  wire [31:0] bit_extender_1_out, rodata_section_data, subtractor_1_out;

  Subtractor #(.width(32)) subtractor_1 (
    .a(Address), .b(32'h10000000), .out(subtractor_1_out), .bout(subtractor_1_bout));  // open: bin
  or or_1 (or_1_out, subtractor_1_out[0], subtractor_1_out[1]);
  or or_2 (InvalidAddressFlag, subtractor_1_bout, subtractor_1_out[31], subtractor_1_out[30], subtractor_1_out[29], subtractor_1_out[28], subtractor_1_out[27], subtractor_1_out[26], and_1_out);
  and and_1 (and_1_out, ~IsReadingByte, or_1_out);  // AND_Gate
  ROM #(.addrWidth(24), .dataWidth(32)) rodata_section (.addr(subtractor_1_out[25:2]), .data(rodata_section_data));
  Multiplexer #(.select(2), .width(8)) multiplexer_1 (
    .in0(rodata_section_data[31:24]), .in1(rodata_section_data[23:16]), .in2(rodata_section_data[15:8]),
    .in3(rodata_section_data[7:0]), .out(multiplexer_1_out), .sel(subtractor_1_out[1:0]));
  assign bit_extender_1_out = {{24{multiplexer_1_out[7]}}, multiplexer_1_out};  // Bit_Extender bit_extender_1
  Multiplexer #(.width(32)) multiplexer_2 (
    .in0({rodata_section_data[7:0], rodata_section_data[15:8], rodata_section_data[23:16], rodata_section_data[31:24]}),
    .in1(bit_extender_1_out), .out(Data), .sel(IsReadingByte));

  // Notes on the sheet:
  //   Data Section Memory Range:
  //   0x1000 0000 - 0x13ff ffff
  //   **Note: this memory is READ ONLY
  //   starting address is 0x0
  //   Offset to where segment
  //   Address[2:25]
  //   (Word Address)
  //   InvalidAddressFlag = 1
  //   If not reading byte and not word aligned,
  //   contents of rodata_section (hex, n*v repeats v):
  //   52657375 6c74203d 20000000 1000000 2000000 3000000 4000000 5000000
  //   **IMPORTANT: Files produced by the associated program
  //   must be decoded with Big-Endian selected.
  //   ^^^ Reverses order of bytes since memory
  //   is encoded as Little-Endian values.
  //   IsReadingByte:
  //   0 - Data = Word starting at Address
  //   1 - Data = Sign-extended byte at Address
endmodule

module DataSection (
  input  [3:0] MemOp,
  input  [31:0] Address,
  input  [31:0] DataIn,
  input  CLK,
  output [31:0] DataOut,
  output InvalidAddressFlag
);

  wire and_1_out, and_2_out, and_3_out, nand_1_out, nand_2_out, nand_3_out, not_1_out;
  wire [1:0] xor_1_out, xor_2_out;
  wire [3:0] multiplexer_1_out;
  wire [4:3] subtractor_1_out_2;
  wire [7:0] multiplexer_3_out, ram_1_dout, ram_1_dout_2, ram_1_dout_3, ram_1_dout_4;
  wire [15:0] multiplexer_4_out;
  wire [31:0] bit_extender_1_out, bit_extender_2_out, bit_extender_3_out, bit_extender_4_out,
       multiplexer_2_out, multiplexer_5_out, multiplexer_6_out, multiplexer_7_out, multiplexer_8_out,
       shifter_1_out, shifter_2_out, shifter_3_out, shifter_4_out;
  wire [31:2] subtractor_1_out;

  Subtractor #(.width(32)) subtractor_1 (
    .a(Address), .b(32'h10000000), .out({subtractor_1_out, subtractor_1_out_2}));  // open: bin, bout
  not not_1 (not_1_out, MemOp[3]);
  and and_1 (and_1_out, subtractor_1_out_2[4], ~MemOp[2], MemOp[1], ~MemOp[0]);  // AND_Gate
  nand nand_1 (nand_1_out, MemOp[2], MemOp[3]);
  nand nand_2 (nand_2_out, MemOp[2], MemOp[3]);
  and and_2 (and_2_out, subtractor_1_out_2[4], nand_1_out, MemOp[1], ~MemOp[0]);  // AND_Gate
  and and_3 (and_3_out, subtractor_1_out_2[3], nand_2_out, ~MemOp[1], MemOp[0]);  // AND_Gate
  or or_1 (InvalidAddressFlag, and_1_out, and_2_out, and_3_out, subtractor_1_out[26], subtractor_1_out[27], subtractor_1_out[28], subtractor_1_out[29], subtractor_1_out[30], subtractor_1_out[31]);
  assign xor_1_out = 2'b11 ^ subtractor_1_out_2;  // XOR_Gate xor_1, 2 bits wide
  Shifter #(.width(32)) shifter_1 (
    .in({DataIn[7:0], DataIn[15:8], DataIn[23:16], DataIn[31:24]}), .\dist ({xor_1_out, 3'b000}),
    .out(shifter_1_out));
  Shifter #(.shift("lr"), .width(32)) shifter_2 (
    .in({DataIn[7:0], DataIn[15:8], DataIn[23:16], DataIn[31:24]}), .\dist ({subtractor_1_out_2, 3'b000}),
    .out(shifter_2_out));
  Multiplexer #(.select(5), .width(4)) multiplexer_1 (
    .in0(4'b1000), .in1(4'b1100), .in2(4'b1111), .in3(4'b0000), .in4(4'b0000), .in5(4'b0000), .in6(4'b1000),
    .in7(4'b1111), .in8(4'b0100), .in9(4'b0000), .in10(4'b0000), .in11(4'b0000), .in12(4'b0000),
    .in13(4'b0000), .in14(4'b1100), .in15(4'b1110), .in16(4'b0010), .in17(4'b0011), .in18(4'b0000),
    .in19(4'b0000), .in20(4'b0000), .in21(4'b0000), .in22(4'b1110), .in23(4'b0011), .in24(4'b0001),
    .in25(4'b0000), .in26(4'b0000), .in27(4'b0000), .in28(4'b0000), .in29(4'b0000), .in30(4'b1111),
    .in31(4'b0001), .out(multiplexer_1_out), .sel({subtractor_1_out_2, MemOp[2:0]}));
  nand nand_3 (nand_3_out, MemOp[2], MemOp[1], MemOp[0]);
  Multiplexer #(.width(32)) multiplexer_2 (
    .in0(shifter_1_out), .in1(shifter_2_out), .out(multiplexer_2_out), .sel(nand_3_out));
  RAM #(.addrWidth(24), .asyncread("true"), .byteenables("byteEnables"), .dataWidth(32), .trigger("falling"), .\type ("nonvolatile")) ram_1 (
    .addr(subtractor_1_out[25:2]), .we(MemOp[3]), .oe(not_1_out), .clk(CLK), .din(multiplexer_2_out),
    .dout({ram_1_dout, ram_1_dout_2, ram_1_dout_3, ram_1_dout_4}), .be3(multiplexer_1_out[3]),
    .be2(multiplexer_1_out[2]), .be1(multiplexer_1_out[1]), .be0(multiplexer_1_out[0]));
  Multiplexer #(.select(2), .width(8)) multiplexer_3 (
    .in0(ram_1_dout), .in1(ram_1_dout_2), .in2(ram_1_dout_3), .in3(ram_1_dout_4), .out(multiplexer_3_out),
    .sel(subtractor_1_out_2));
  Multiplexer #(.select(2), .width(16)) multiplexer_4 (
    .in0({ram_1_dout_4, ram_1_dout_3}), .in2({ram_1_dout_2, ram_1_dout}), .out(multiplexer_4_out),
    .sel(subtractor_1_out_2));  // open: in1, in3
  assign xor_2_out = 2'b11 ^ subtractor_1_out_2;  // XOR_Gate xor_2, 2 bits wide
  assign bit_extender_1_out = {{24{multiplexer_3_out[7]}}, multiplexer_3_out};  // Bit_Extender bit_extender_1
  assign bit_extender_2_out = {{24{1'b0}}, multiplexer_3_out};  // Bit_Extender bit_extender_2
  assign bit_extender_3_out = {{16{multiplexer_4_out[15]}}, multiplexer_4_out};  // Bit_Extender bit_extender_3
  assign bit_extender_4_out = {{16{1'b0}}, multiplexer_4_out};  // Bit_Extender bit_extender_4
  Shifter #(.width(32)) shifter_3 (
    .in({ram_1_dout_4, ram_1_dout_3, ram_1_dout_2, ram_1_dout}), .\dist ({xor_2_out, 3'b000}),
    .out(shifter_3_out));
  Multiplexer #(.width(32)) multiplexer_5 (
    .in0(bit_extender_1_out), .in1(bit_extender_2_out), .out(multiplexer_5_out), .sel(MemOp[2]));
  Multiplexer #(.width(32)) multiplexer_6 (
    .in0(bit_extender_3_out), .in1(bit_extender_4_out), .out(multiplexer_6_out), .sel(MemOp[2]));
  Shifter #(.shift("lr"), .width(32)) shifter_4 (
    .in({ram_1_dout_4, ram_1_dout_3, ram_1_dout_2, ram_1_dout}), .\dist ({subtractor_1_out_2, 3'b000}),
    .out(shifter_4_out));
  Multiplexer #(.width(32)) multiplexer_7 (
    .in0({ram_1_dout_4, ram_1_dout_3, ram_1_dout_2, ram_1_dout}), .in1(shifter_3_out),
    .out(multiplexer_7_out), .sel(MemOp[2]));
  Multiplexer #(.width(32)) multiplexer_8 (
    .in0({32{1'b0}}), .in1(shifter_4_out), .out(multiplexer_8_out), .sel(MemOp[2]));
  Multiplexer #(.select(2), .width(32)) multiplexer_9 (
    .in0(multiplexer_5_out), .in1(multiplexer_6_out), .in2(multiplexer_7_out), .in3(multiplexer_8_out),
    .out(DataOut), .sel(MemOp[1:0]));

  // Notes on the sheet:
  //   Data Section Memory Range:
  //   0x1000 0000 - 0x13ff ffff
  //   **IMPORTANT: Uses Little-Endian
  //   byte order for words
  //   InvalidAddressFlag:
  //   0 - Valid Address
  //   MemOp Codes:
  //   0000 - lb
  //   0001 - lh
  //   0010 - lw
  //   0011 - N/A
  //   0100 - lbu
  //   0101 - lhu
  //   0110 - lwl
  //   0111 - lwr
  //   1. Address out of range
  //   1000 - sb
  //   1001 - sh
  //   1010 - sw
  //   1 - Invalid Address for any of the following reasons:
  //   1011 - N/A
  //   1100 - N/A
  //   1101 - N/A
  //   1110 - swl
  //   1111 - swr
  //   unless is swr instruction.
  //   2. Attempting to write/read a non-word aligned word
  //   3. Attempting to write/read a non-halfword aligned halfword
  //   Shifts logical right by Address % 4 bytes
  //   <- Write Enable
  //   <- Read Enable
  //   <- Pre-programmed byte mask for writing
  //   <<=======
  //   <<=======
  //   LOAD bin/data FILE HERE!
  //   RIGHT CLICK RAM:
  //   Load Image > bin/data
  //   **Leave it decoding in Big-Endian**
  //   lb/lbu
  //   lh/lhu
  //   lw/lwl
  //   nop/lwr
  //   Formats output data based on type of load instruction
endmodule

module StackSection (
  input  [3:0] MemOp,
  input  [31:0] Address,
  input  [31:0] DataIn,
  input  CLK,
  output [31:0] DataOut,
  output InvalidAddressFlag
);

  wire and_1_out, and_2_out, and_3_out, nand_1_out, nand_2_out, nand_3_out, not_1_out;
  wire [1:0] xor_1_out, xor_2_out;
  wire [3:0] multiplexer_1_out;
  wire [4:3] subtractor_1_out_2;
  wire [7:0] multiplexer_3_out, ram_1_dout, ram_1_dout_2, ram_1_dout_3, ram_1_dout_4;
  wire [15:0] multiplexer_4_out;
  wire [31:0] bit_extender_1_out, bit_extender_2_out, bit_extender_3_out, bit_extender_4_out,
       multiplexer_2_out, multiplexer_5_out, multiplexer_6_out, multiplexer_7_out, multiplexer_8_out,
       shifter_1_out, shifter_2_out, shifter_3_out, shifter_4_out;
  wire [31:2] subtractor_1_out;

  Subtractor #(.width(32)) subtractor_1 (
    .a(Address), .b(32'h7c000000), .out({subtractor_1_out, subtractor_1_out_2}));  // open: bin, bout
  not not_1 (not_1_out, MemOp[3]);
  and and_1 (and_1_out, subtractor_1_out_2[4], ~MemOp[2], MemOp[1], ~MemOp[0]);  // AND_Gate
  nand nand_1 (nand_1_out, MemOp[2], MemOp[3]);
  nand nand_2 (nand_2_out, MemOp[2], MemOp[3]);
  and and_2 (and_2_out, subtractor_1_out_2[4], nand_1_out, MemOp[1], ~MemOp[0]);  // AND_Gate
  and and_3 (and_3_out, subtractor_1_out_2[3], nand_2_out, ~MemOp[1], MemOp[0]);  // AND_Gate
  or or_1 (InvalidAddressFlag, and_1_out, and_2_out, and_3_out, subtractor_1_out[26], subtractor_1_out[27], subtractor_1_out[28], subtractor_1_out[29], subtractor_1_out[30], subtractor_1_out[31]);
  assign xor_1_out = 2'b11 ^ subtractor_1_out_2;  // XOR_Gate xor_1, 2 bits wide
  Shifter #(.width(32)) shifter_1 (
    .in({DataIn[7:0], DataIn[15:8], DataIn[23:16], DataIn[31:24]}), .\dist ({xor_1_out, 3'b000}),
    .out(shifter_1_out));
  Shifter #(.shift("lr"), .width(32)) shifter_2 (
    .in({DataIn[7:0], DataIn[15:8], DataIn[23:16], DataIn[31:24]}), .\dist ({subtractor_1_out_2, 3'b000}),
    .out(shifter_2_out));
  Multiplexer #(.select(5), .width(4)) multiplexer_1 (
    .in0(4'b1000), .in1(4'b1100), .in2(4'b1111), .in3(4'b0000), .in4(4'b0000), .in5(4'b0000), .in6(4'b1000),
    .in7(4'b1111), .in8(4'b0100), .in9(4'b0000), .in10(4'b0000), .in11(4'b0000), .in12(4'b0000),
    .in13(4'b0000), .in14(4'b1100), .in15(4'b1110), .in16(4'b0010), .in17(4'b0011), .in18(4'b0000),
    .in19(4'b0000), .in20(4'b0000), .in21(4'b0000), .in22(4'b1110), .in23(4'b0011), .in24(4'b0001),
    .in25(4'b0000), .in26(4'b0000), .in27(4'b0000), .in28(4'b0000), .in29(4'b0000), .in30(4'b1111),
    .in31(4'b0001), .out(multiplexer_1_out), .sel({subtractor_1_out_2, MemOp[2:0]}));
  nand nand_3 (nand_3_out, MemOp[2], MemOp[1], MemOp[0]);
  Multiplexer #(.width(32)) multiplexer_2 (
    .in0(shifter_1_out), .in1(shifter_2_out), .out(multiplexer_2_out), .sel(nand_3_out));
  RAM #(.addrWidth(24), .asyncread("true"), .byteenables("byteEnables"), .dataWidth(32), .trigger("falling"), .\type ("nonvolatile")) ram_1 (
    .addr(subtractor_1_out[25:2]), .we(MemOp[3]), .oe(not_1_out), .clk(CLK), .din(multiplexer_2_out),
    .dout({ram_1_dout, ram_1_dout_2, ram_1_dout_3, ram_1_dout_4}), .be3(multiplexer_1_out[3]),
    .be2(multiplexer_1_out[2]), .be1(multiplexer_1_out[1]), .be0(multiplexer_1_out[0]));
  Multiplexer #(.select(2), .width(8)) multiplexer_3 (
    .in0(ram_1_dout), .in1(ram_1_dout_2), .in2(ram_1_dout_3), .in3(ram_1_dout_4), .out(multiplexer_3_out),
    .sel(subtractor_1_out_2));
  Multiplexer #(.select(2), .width(16)) multiplexer_4 (
    .in0({ram_1_dout_4, ram_1_dout_3}), .in2({ram_1_dout_2, ram_1_dout}), .out(multiplexer_4_out),
    .sel(subtractor_1_out_2));  // open: in1, in3
  assign xor_2_out = 2'b11 ^ subtractor_1_out_2;  // XOR_Gate xor_2, 2 bits wide
  assign bit_extender_1_out = {{24{multiplexer_3_out[7]}}, multiplexer_3_out};  // Bit_Extender bit_extender_1
  assign bit_extender_2_out = {{24{1'b0}}, multiplexer_3_out};  // Bit_Extender bit_extender_2
  assign bit_extender_3_out = {{16{multiplexer_4_out[15]}}, multiplexer_4_out};  // Bit_Extender bit_extender_3
  assign bit_extender_4_out = {{16{1'b0}}, multiplexer_4_out};  // Bit_Extender bit_extender_4
  Shifter #(.width(32)) shifter_3 (
    .in({ram_1_dout_4, ram_1_dout_3, ram_1_dout_2, ram_1_dout}), .\dist ({xor_2_out, 3'b000}),
    .out(shifter_3_out));
  Multiplexer #(.width(32)) multiplexer_5 (
    .in0(bit_extender_1_out), .in1(bit_extender_2_out), .out(multiplexer_5_out), .sel(MemOp[2]));
  Multiplexer #(.width(32)) multiplexer_6 (
    .in0(bit_extender_3_out), .in1(bit_extender_4_out), .out(multiplexer_6_out), .sel(MemOp[2]));
  Shifter #(.shift("lr"), .width(32)) shifter_4 (
    .in({ram_1_dout_4, ram_1_dout_3, ram_1_dout_2, ram_1_dout}), .\dist ({subtractor_1_out_2, 3'b000}),
    .out(shifter_4_out));
  Multiplexer #(.width(32)) multiplexer_7 (
    .in0({ram_1_dout_4, ram_1_dout_3, ram_1_dout_2, ram_1_dout}), .in1(shifter_3_out),
    .out(multiplexer_7_out), .sel(MemOp[2]));
  Multiplexer #(.width(32)) multiplexer_8 (
    .in0({32{1'b0}}), .in1(shifter_4_out), .out(multiplexer_8_out), .sel(MemOp[2]));
  Multiplexer #(.select(2), .width(32)) multiplexer_9 (
    .in0(multiplexer_5_out), .in1(multiplexer_6_out), .in2(multiplexer_7_out), .in3(multiplexer_8_out),
    .out(DataOut), .sel(MemOp[1:0]));

  // Notes on the sheet:
  //   Stack Section Memory Range:
  //   0x7c00 0000 - 7fff ffff
  //   **IMPORTANT: Uses Little-Endian
  //   byte order for words
  //   InvalidAddressFlag:
  //   0 - Valid Address
  //   MemOp Codes:
  //   0000 - lb
  //   0001 - lh
  //   0010 - lw
  //   0011 - N/A
  //   0100 - lbu
  //   0101 - lhu
  //   0110 - lwl
  //   0111 - lwr
  //   1. Address out of range
  //   1000 - sb
  //   1001 - sh
  //   1010 - sw
  //   1 - Invalid Address for any of the following reasons:
  //   1011 - N/A
  //   1100 - N/A
  //   1101 - N/A
  //   1110 - swl
  //   1111 - swr
  //   unless is swr instruction.
  //   2. Attempting to write/read a non-word aligned word
  //   3. Attempting to write/read a non-halfword aligned halfword
  //   Shifts logical right by Address % 4 bytes
  //   <- Write Enable
  //   <- Read Enable
  //   <- Pre-programmed byte mask for writing
  //   lb/lbu
  //   lh/lhu
  //   lw/lwl
  //   nop/lwr
  //   Formats output data based on type of load instruction
endmodule

module ALU (
  input  [3:0] ALUControl,
  input  [31:0] A,
  input  [31:0] B,
  input  NOT_ALUOutput,
  output [31:0] Q
);

  wire adder_1_cout, and_3_out, and_5_out, and_7_out, and_9_out, and_11_out, and_13_out, and_15_out,
       and_17_out, and_19_out, and_21_out, and_23_out, and_25_out, and_27_out, and_29_out, and_31_out,
       and_33_out, comparator_1_lt, comparator_2_lt, subtractor_1_bout;
  wire [31:0] adder_1_out, adder_2_out, and_1_out, and_2_out, and_4_out, and_6_out, and_8_out, and_10_out,
       and_12_out, and_14_out, and_16_out, and_18_out, and_20_out, and_22_out, and_24_out, and_26_out,
       and_28_out, and_30_out, and_32_out, bit_extender_1_out, bit_extender_2_out, bit_extender_3_out,
       bit_extender_4_out, bit_extender_5_out, bit_extender_6_out, bit_extender_7_out, bit_extender_8_out,
       bit_extender_9_out, bit_extender_10_out, bit_extender_11_out, bit_extender_12_out,
       bit_extender_13_out, bit_extender_14_out, bit_extender_15_out, bit_extender_16_out,
       bit_extender_17_out, bit_extender_18_out, divider_1_out, divider_2_out, multiplier_1_out,
       multiplier_2_out, or_1_out, or_2_out, or_3_out, or_4_out, or_5_out, or_6_out, or_7_out, or_8_out,
       or_9_out, or_10_out, or_11_out, or_12_out, or_13_out, or_14_out, or_15_out, or_16_out, or_17_out,
       shifter_1_out, shifter_2_out, shifter_3_out, subtractor_1_out, subtractor_2_out, xor_1_out, xor_2_out;

  Multiplexer #(.width(32)) multiplexer_1 (.in0(or_1_out), .in1(xor_1_out), .out(Q), .sel(NOT_ALUOutput));
  assign xor_1_out = or_1_out ^ {32{1'b1}};  // XOR_Gate xor_1, 32 bits wide
  assign and_1_out = A & B;  // AND_Gate and_1, 32 bits wide
  assign or_1_out = or_3_out | and_2_out;  // OR_Gate or_1, 32 bits wide
  assign and_2_out = and_1_out & bit_extender_1_out;  // AND_Gate and_2, 32 bits wide
  and and_3 (and_3_out, ~ALUControl[3], ~ALUControl[2], ~ALUControl[1], ~ALUControl[0]);  // AND_Gate
  assign bit_extender_1_out = {{31{and_3_out}}, and_3_out};  // Bit_Extender bit_extender_1
  assign or_2_out = A | B;  // OR_Gate or_2, 32 bits wide
  assign or_3_out = or_4_out | and_4_out;  // OR_Gate or_3, 32 bits wide
  assign and_4_out = or_2_out & bit_extender_2_out;  // AND_Gate and_4, 32 bits wide
  and and_5 (and_5_out, ~ALUControl[3], ~ALUControl[2], ~ALUControl[1], ALUControl[0]);  // AND_Gate
  assign bit_extender_2_out = {{31{and_5_out}}, and_5_out};  // Bit_Extender bit_extender_2
  assign xor_2_out = A ^ B;  // XOR_Gate xor_2, 32 bits wide
  assign or_4_out = or_5_out | and_6_out;  // OR_Gate or_4, 32 bits wide
  assign and_6_out = xor_2_out & bit_extender_3_out;  // AND_Gate and_6, 32 bits wide
  and and_7 (and_7_out, ~ALUControl[3], ~ALUControl[2], ALUControl[1], ~ALUControl[0]);  // AND_Gate
  assign bit_extender_3_out = {{31{and_7_out}}, and_7_out};  // Bit_Extender bit_extender_3
  Shifter #(.width(32)) shifter_1 (.in(A), .\dist (B[4:0]), .out(shifter_1_out));
  assign or_5_out = or_6_out | and_8_out;  // OR_Gate or_5, 32 bits wide
  assign and_8_out = shifter_1_out & bit_extender_4_out;  // AND_Gate and_8, 32 bits wide
  and and_9 (and_9_out, ~ALUControl[3], ~ALUControl[2], ALUControl[1], ALUControl[0]);  // AND_Gate
  assign bit_extender_4_out = {{31{and_9_out}}, and_9_out};  // Bit_Extender bit_extender_4
  Shifter #(.shift("lr"), .width(32)) shifter_2 (.in(A), .\dist (B[4:0]), .out(shifter_2_out));
  assign or_6_out = or_7_out | and_10_out;  // OR_Gate or_6, 32 bits wide
  assign and_10_out = shifter_2_out & bit_extender_5_out;  // AND_Gate and_10, 32 bits wide
  and and_11 (and_11_out, ~ALUControl[3], ALUControl[2], ~ALUControl[1], ~ALUControl[0]);  // AND_Gate
  assign bit_extender_5_out = {{31{and_11_out}}, and_11_out};  // Bit_Extender bit_extender_5
  assign or_7_out = or_8_out | and_12_out;  // OR_Gate or_7, 32 bits wide
  Shifter #(.shift("ar"), .width(32)) shifter_3 (.in(A), .\dist (B[4:0]), .out(shifter_3_out));
  assign and_12_out = shifter_3_out & bit_extender_6_out;  // AND_Gate and_12, 32 bits wide
  and and_13 (and_13_out, ~ALUControl[3], ALUControl[2], ~ALUControl[1], ALUControl[0]);  // AND_Gate
  assign bit_extender_6_out = {{31{and_13_out}}, and_13_out};  // Bit_Extender bit_extender_6
  Adder #(.width(32)) adder_1 (.a(A), .b(B), .out(adder_1_out), .cout(adder_1_cout));  // open: cin
  assign or_8_out = or_9_out | and_14_out;  // OR_Gate or_8, 32 bits wide
  assign and_14_out = adder_1_out & bit_extender_7_out;  // AND_Gate and_14, 32 bits wide
  and and_15 (and_15_out, ~ALUControl[3], ALUControl[2], ALUControl[1], ~ALUControl[0]);  // AND_Gate
  assign bit_extender_7_out = {{31{and_15_out}}, and_15_out};  // Bit_Extender bit_extender_7
  Adder #(.width(32)) adder_2 (.a(A), .b(B), .out(adder_2_out));  // open: cin, cout
  assign or_9_out = or_10_out | and_16_out;  // OR_Gate or_9, 32 bits wide
  assign and_16_out = adder_2_out & bit_extender_8_out;  // AND_Gate and_16, 32 bits wide
  and and_17 (and_17_out, ~ALUControl[3], ALUControl[2], ALUControl[1], ALUControl[0]);  // AND_Gate
  assign bit_extender_8_out = {{31{and_17_out}}, and_17_out};  // Bit_Extender bit_extender_8
  Subtractor #(.width(32)) subtractor_1 (.a(A), .b(B), .out(subtractor_1_out), .bout(subtractor_1_bout));  // open: bin
  assign or_10_out = or_11_out | and_18_out;  // OR_Gate or_10, 32 bits wide
  assign and_18_out = subtractor_1_out & bit_extender_9_out;  // AND_Gate and_18, 32 bits wide
  and and_19 (and_19_out, ALUControl[3], ~ALUControl[2], ~ALUControl[1], ~ALUControl[0]);  // AND_Gate
  assign bit_extender_9_out = {{31{and_19_out}}, and_19_out};  // Bit_Extender bit_extender_9
  Subtractor #(.width(32)) subtractor_2 (.a(A), .b(B), .out(subtractor_2_out));  // open: bin, bout
  assign or_11_out = or_12_out | and_20_out;  // OR_Gate or_11, 32 bits wide
  assign and_20_out = subtractor_2_out & bit_extender_10_out;  // AND_Gate and_20, 32 bits wide
  and and_21 (and_21_out, ALUControl[3], ~ALUControl[2], ~ALUControl[1], ALUControl[0]);  // AND_Gate
  assign bit_extender_10_out = {{31{and_21_out}}, and_21_out};  // Bit_Extender bit_extender_10
  Multiplier #(.mode("twosComplement"), .width(32)) multiplier_1 (
    .a(A), .b(B), .out(multiplier_1_out));  // open: cin, cout
  assign or_12_out = or_13_out | and_22_out;  // OR_Gate or_12, 32 bits wide
  assign and_22_out = multiplier_1_out & bit_extender_11_out;  // AND_Gate and_22, 32 bits wide
  and and_23 (and_23_out, ALUControl[3], ~ALUControl[2], ALUControl[1], ~ALUControl[0]);  // AND_Gate
  assign bit_extender_11_out = {{31{and_23_out}}, and_23_out};  // Bit_Extender bit_extender_11
  Multiplier #(.width(32)) multiplier_2 (.a(A), .b(B), .out(multiplier_2_out));  // open: cin, cout
  assign or_13_out = or_14_out | and_24_out;  // OR_Gate or_13, 32 bits wide
  assign and_24_out = multiplier_2_out & bit_extender_12_out;  // AND_Gate and_24, 32 bits wide
  and and_25 (and_25_out, ALUControl[3], ~ALUControl[2], ALUControl[1], ALUControl[0]);  // AND_Gate
  assign bit_extender_12_out = {{31{and_25_out}}, and_25_out};  // Bit_Extender bit_extender_12
  Divider #(.mode("twosComplement"), .width(32)) divider_1 (.a(A), .b(B), .out(divider_1_out));  // open: upper, rem
  assign or_14_out = or_15_out | and_26_out;  // OR_Gate or_14, 32 bits wide
  assign and_26_out = divider_1_out & bit_extender_13_out;  // AND_Gate and_26, 32 bits wide
  and and_27 (and_27_out, ALUControl[3], ALUControl[2], ~ALUControl[1], ~ALUControl[0]);  // AND_Gate
  assign bit_extender_13_out = {{31{and_27_out}}, and_27_out};  // Bit_Extender bit_extender_13
  Divider #(.width(32)) divider_2 (.a(A), .b(B), .out(divider_2_out));  // open: upper, rem
  assign or_15_out = or_16_out | and_28_out;  // OR_Gate or_15, 32 bits wide
  assign and_28_out = divider_2_out & bit_extender_14_out;  // AND_Gate and_28, 32 bits wide
  and and_29 (and_29_out, ALUControl[3], ALUControl[2], ~ALUControl[1], ALUControl[0]);  // AND_Gate
  assign bit_extender_14_out = {{31{and_29_out}}, and_29_out};  // Bit_Extender bit_extender_14
  Comparator #(.width(32)) comparator_1 (.a(A), .b(B), .lt(comparator_1_lt));  // open: gt, eq
  assign or_16_out = or_17_out | and_30_out;  // OR_Gate or_16, 32 bits wide
  assign and_30_out = bit_extender_15_out & bit_extender_16_out;  // AND_Gate and_30, 32 bits wide
  assign bit_extender_15_out = {{31{1'b0}}, comparator_1_lt};  // Bit_Extender bit_extender_15
  and and_31 (and_31_out, ALUControl[3], ALUControl[2], ALUControl[1], ~ALUControl[0]);  // AND_Gate
  assign bit_extender_16_out = {{31{and_31_out}}, and_31_out};  // Bit_Extender bit_extender_16
  Comparator #(.mode("unsigned"), .width(32)) comparator_2 (.a(A), .b(B), .lt(comparator_2_lt));  // open: gt, eq
  assign or_17_out = {32{1'b0}} | and_32_out;  // OR_Gate or_17, 32 bits wide
  assign and_32_out = bit_extender_17_out & bit_extender_18_out;  // AND_Gate and_32, 32 bits wide
  assign bit_extender_17_out = {{31{1'b0}}, comparator_2_lt};  // Bit_Extender bit_extender_17
  and and_33 (and_33_out, ALUControl[3], ALUControl[2], ALUControl[1], ALUControl[0]);
  assign bit_extender_18_out = {{31{and_33_out}}, and_33_out};  // Bit_Extender bit_extender_18

  // Notes on the sheet:
  //   Key:
  //   0000 - A & B
  //   0001 - A | B
  //   0010 - A ^ B
  //   0110 - A + B
  //   1000 - A - B
  //   1010 - A * B
  //   1100 - A / B
  //   1110 - slt Q, A, B
  //   1111 - sltu Q, A, B
  //   0011 - A << B (logical)
  //   0100 - A >> B (logical)
  //   0101 - A >> B (arith.)
  //   0111 - A + B (unsigned)
  //   1001 - A - B (unsigned)
  //   1011 - A * B (unsigned)
  //   1101 - A / B (unsigned)
  //   0000 - A & B
  //   0001 - A | B
  //   0010 - A ^ B
  //   0011 - A << B (sll)
  //   0100 - A >> B (srl)
  //   0101 - A >> B (sra)
  //   0110 - A + B
  //   Overflow
  //   0111 - A + B (addu)
  //   1000 - A - B
  //   Overflow
  //   1001 - A - B (subu)
  //   1010 - A * B
  //   1011 - A * B (unsigned)
  //   1100 - A / B
  //   1101 - A / B (unsigned)
  //   1110 - slt Q, A, B
  //   1111 - sltu Q, A, B
endmodule

module DataPathRegister1 (
  input  [31:0] InstrF,
  input  [31:0] PCPlus4F,
  input  CLK,
  input  Reset,
  output [31:0] InstrD,
  output [31:0] PCPlus4D
);

  Register #(.width(32)) register_1 (.D(InstrF), .clk(CLK), .Q(InstrD), .clr(Reset));  // open: en
  Register #(.width(32)) register_2 (.D(PCPlus4F), .clk(CLK), .Q(PCPlus4D), .clr(Reset));  // open: en
endmodule

module DataPathRegister2 (
  input  [31:0] RegData1D,
  input  [31:0] RegData2D,
  input  [4:0] r_rt_D,
  input  [4:0] r_rd_D,
  input  [31:0] SignImmD,
  input  [31:0] PCPlus4D,
  input  CLK,
  input  Reset,
  output [31:0] RegData1E,
  output [31:0] RegData2E,
  output [4:0] r_rt_E,
  output [4:0] r_rd_E,
  output [31:0] SignImmE,
  output [31:0] PCPlus4E
);

  Register #(.width(32)) register_1 (.D(RegData1D), .clk(CLK), .Q(RegData1E), .clr(Reset));  // open: en
  Register #(.width(32)) register_2 (.D(RegData2D), .clk(CLK), .Q(RegData2E), .clr(Reset));  // open: en
  Register #(.width(5)) register_3 (.D(r_rt_D), .clk(CLK), .Q(r_rt_E), .clr(Reset));  // open: en
  Register #(.width(5)) register_4 (.D(r_rd_D), .clk(CLK), .Q(r_rd_E), .clr(Reset));  // open: en
  Register #(.width(32)) register_5 (.D(SignImmD), .clk(CLK), .Q(SignImmE), .clr(Reset));  // open: en
  Register #(.width(32)) register_6 (.D(PCPlus4D), .clk(CLK), .Q(PCPlus4E), .clr(Reset));  // open: en
endmodule

module DataPathRegister3 (
  input  [31:0] ALUOutE,
  input  [31:0] UpperImmE,
  input  [31:0] WriteDataE,
  input  [4:0] WriteRegE,
  input  [31:0] PCBranchE,
  input  CLK,
  input  Reset,
  output ZeroM,
  output [31:0] ALUOutM,
  output [31:0] UpperImmM,
  output [31:0] WriteDataM,
  output [4:0] WriteRegM,
  output [31:0] PCBranchM
);

  wire comparator_1_eq;

  Comparator #(.width(32)) comparator_1 (.a({32{1'b0}}), .b(ALUOutE), .eq(comparator_1_eq));  // open: gt, lt
  Register #(.width(1)) register_1 (.D(comparator_1_eq), .clk(CLK), .Q(ZeroM), .clr(Reset));  // open: en
  Register #(.width(32)) register_2 (.D(ALUOutE), .clk(CLK), .Q(ALUOutM), .clr(Reset));  // open: en
  Register #(.width(32)) register_3 (.D(UpperImmE), .clk(CLK), .Q(UpperImmM), .clr(Reset));  // open: en
  Register #(.width(32)) register_4 (.D(WriteDataE), .clk(CLK), .Q(WriteDataM), .clr(Reset));  // open: en
  Register #(.width(5)) register_5 (.D(WriteRegE), .clk(CLK), .Q(WriteRegM), .clr(Reset));  // open: en
  Register #(.width(32)) register_6 (.D(PCBranchE), .clk(CLK), .Q(PCBranchM), .clr(Reset));  // open: en
endmodule

module DataPathRegister4 (
  input  [31:0] ALUOutM,
  input  [31:0] UpperImmM,
  input  [31:0] ReadDataM,
  input  [4:0] WriteRegM,
  input  CLK,
  input  Reset,
  output [31:0] ALUOutW,
  output [31:0] UpperImmW,
  output [31:0] ReadDataW,
  output [4:0] WriteRegW
);

  Register #(.width(32)) register_1 (.D(ALUOutM), .clk(CLK), .Q(ALUOutW), .clr(Reset));  // open: en
  Register #(.width(32)) register_2 (.D(UpperImmM), .clk(CLK), .Q(UpperImmW), .clr(Reset));  // open: en
  Register #(.width(32)) register_3 (.D(ReadDataM), .clk(CLK), .Q(ReadDataW), .clr(Reset));  // open: en
  Register #(.width(5)) register_4 (.D(WriteRegM), .clk(CLK), .Q(WriteRegW), .clr(Reset));  // open: en
endmodule

module ControlPathRegister2 (
  input  RegWriteD,
  input  [1:0] MemToRegD,
  input  [3:0] MemOpD,
  input  BranchD,
  input  [3:0] ALUControlD,
  input  [1:0] ALUSrcD,
  input  RegDstD,
  input  CLK,
  input  Reset,
  output RegWriteE,
  output [1:0] MemToRegE,
  output [3:0] MemOpE,
  output BranchE,
  output [3:0] ALUControlE,
  output [1:0] ALUSrcE,
  output RegDstE
);

  Register #(.width(1)) register_1 (.D(RegWriteD), .clk(CLK), .Q(RegWriteE), .clr(Reset));  // open: en
  Register #(.width(2)) register_2 (.D(MemToRegD), .clk(CLK), .Q(MemToRegE), .clr(Reset));  // open: en
  Register #(.width(4)) register_3 (.D(MemOpD), .clk(CLK), .Q(MemOpE), .clr(Reset));  // open: en
  Register #(.width(1)) register_4 (.D(BranchD), .clk(CLK), .Q(BranchE), .clr(Reset));  // open: en
  Register #(.width(4)) register_5 (.D(ALUControlD), .clk(CLK), .Q(ALUControlE), .clr(Reset));  // open: en
  Register #(.width(2)) register_6 (.D(ALUSrcD), .clk(CLK), .Q(ALUSrcE), .clr(Reset));  // open: en
  Register #(.width(1)) register_7 (.D(RegDstD), .clk(CLK), .Q(RegDstE), .clr(Reset));  // open: en
endmodule

module ControlPathRegister3 (
  input  RegWriteE,
  input  [1:0] MemToRegE,
  input  [3:0] MemOpE,
  input  BranchE,
  input  CLK,
  input  Reset,
  output RegWriteM,
  output [1:0] MemToRegM,
  output [3:0] MemOpM,
  output BranchM
);

  Register #(.width(1)) register_1 (.D(RegWriteE), .clk(CLK), .Q(RegWriteM), .clr(Reset));  // open: en
  Register #(.width(2)) register_2 (.D(MemToRegE), .clk(CLK), .Q(MemToRegM), .clr(Reset));  // open: en
  Register #(.width(4)) register_3 (.D(MemOpE), .clk(CLK), .Q(MemOpM), .clr(Reset));  // open: en
  Register #(.width(1)) register_4 (.D(BranchE), .clk(CLK), .Q(BranchM), .clr(Reset));  // open: en
endmodule

module ControlPathRegister4 (
  input  RegWriteM,
  input  [1:0] MemToRegM,
  input  CLK,
  input  Reset,
  output RegWriteW,
  output [1:0] MemToRegW
);

  Register #(.width(1)) register_1 (.D(RegWriteM), .clk(CLK), .Q(RegWriteW), .clr(Reset));  // open: en
  Register #(.width(2)) register_2 (.D(MemToRegM), .clk(CLK), .Q(MemToRegW), .clr(Reset));  // open: en
endmodule
